// Logisim project pong.circ as structural Verilog: 14 circuits, main circuit main
module main (
);

  wire and_1_out, and_2_out, and_4_out, clk, clock_1_out, clock_2_out, clock_4_out, counter_3_carry, ee,
       en_video, gameOver, la, lb, ld, loose, not_2_out, not_3_out, not_started, or_1_out, or_4_out,
       or_6_out, real_ns, rst, start, video_clk, win;
  wire [0:0] counter_2_q;
  wire [1:0] multiplexer_1_out, multiplexer_2_out, multiplexer_3_out;
  wire [3:0] ten_1_out_2, ten_1_out_3, ten_2_out_2, ten_2_out_3;
  wire [4:0] kinematic_1_ballx, kinematic_1_bally, kinematic_1_leftyout, kinematic_1_rightyout,
       kinematic_1_zero, lx, ly, ry, video_section_1_out_18, video_section_1_out_19, video_section_1_out_20,
       video_section_1_out_21, video_section_1_out_22, video_section_2_out_18, video_section_2_out_19,
       video_section_2_out_20, video_section_2_out_21, video_section_2_out_22, video_section_3_out_18,
       video_section_3_out_19, video_section_3_out_20, video_section_3_out_21, video_section_3_out_22;
  wire [7:0] as, bs, counter_1_q, video_ctrl, video_section_1_controlin_2, video_section_2_controlin_2,
       video_section_3_controlin_2;
  wire [15:0] bx, by, register_1_q, register_2_q, register_3_q, register_4_q, vx, vy;
  wire [31:0] video_data, video_section_1_imagedatain_2, video_section_1_out_8, video_section_1_out_9,
       video_section_1_out_10, video_section_1_out_11, video_section_1_out_13, video_section_1_out_14,
       video_section_1_out_15, video_section_1_out_16, video_section_2_imagedatain_2, video_section_2_out_8,
       video_section_2_out_9, video_section_2_out_10, video_section_2_out_11, video_section_2_out_13,
       video_section_2_out_14, video_section_2_out_15, video_section_2_out_16, video_section_3_imagedatain_2,
       video_section_3_out_8, video_section_3_out_9, video_section_3_out_10, video_section_3_out_11,
       video_section_3_out_13, video_section_3_out_14, video_section_3_out_15, video_section_3_out_16,
       video_section_4_out_8, video_section_4_out_9, video_section_4_out_10, video_section_4_out_11,
       video_section_4_out_13, video_section_4_out_14, video_section_4_out_15, video_section_4_out_16;

  Clock clock_1 (.out(clock_1_out));
  // Gamepad gamepad_1: pin names not known; wires that end beside it: clock_1_out, start, la, lb, lx, ly
  Clock #(.highDuration(2), .lowDuration(2)) clock_2 (.out(clock_2_out));
  Hex_Digit_Display hex_digit_display_1 (.value(ten_1_out_2));  // open: dp
  or or_1 (or_1_out, start, not_started, rst);
  and and_1 (and_1_out, clock_2_out, ~not_started, ~gameOver);  // AND_Gate
  Hex_Digit_Display hex_digit_display_2 (.value(ten_1_out_3));  // open: dp
  ten ten_1 (.in_1(as), .out_2(ten_1_out_2), .out_3(ten_1_out_3));
  DotMatrix #(.matrixcols(32), .matrixrows(32)) dotmatrix_1 (
    .col0(video_section_1_out_13), .col1(video_section_1_out_8), .col2(video_section_1_out_14),
    .col3(video_section_1_out_9), .col4(video_section_1_out_15), .col5(video_section_1_out_10),
    .col6(video_section_1_out_16), .col7(video_section_1_out_11), .col8(video_section_2_out_13),
    .col9(video_section_2_out_8), .col10(video_section_2_out_14), .col11(video_section_2_out_9),
    .col12(video_section_2_out_15), .col13(video_section_2_out_10), .col14(video_section_2_out_16),
    .col15(video_section_2_out_11), .col16(video_section_3_out_13), .col17(video_section_3_out_8),
    .col18(video_section_3_out_14), .col19(video_section_3_out_9), .col20(video_section_3_out_15),
    .col21(video_section_3_out_10), .col22(video_section_3_out_16), .col23(video_section_3_out_11),
    .col24(video_section_4_out_13), .col25(video_section_4_out_8), .col26(video_section_4_out_14),
    .col27(video_section_4_out_9), .col28(video_section_4_out_15), .col29(video_section_4_out_10),
    .col30(video_section_4_out_16), .col31(video_section_4_out_11));
  kinematic kinematic_1 (
    .reset(or_1_out), .leftYin(ly), .rightYin(ry), .leftYout(kinematic_1_leftyout),
    .rightYout(kinematic_1_rightyout), .scoreA(as), .scoreB(bs), .zero(kinematic_1_zero),
    .ballx(kinematic_1_ballx), .bally(kinematic_1_bally), .clock(and_1_out), .bx(bx), .by(by), .vx(vx),
    .vy(vy));
  video_section video_section_1 (
    .chipID(kinematic_1_zero), .ballX(kinematic_1_ballx), .ballY(kinematic_1_bally),
    .leftbatY(kinematic_1_leftyout), .rightbatY(kinematic_1_rightyout), .out_18(video_section_1_out_18),
    .out_19(video_section_1_out_19), .out_20(video_section_1_out_20), .out_21(video_section_1_out_21),
    .out_22(video_section_1_out_22), .out_13(video_section_1_out_13), .out_8(video_section_1_out_8),
    .out_14(video_section_1_out_14), .out_9(video_section_1_out_9), .out_15(video_section_1_out_15),
    .out_10(video_section_1_out_10), .out_16(video_section_1_out_16), .out_11(video_section_1_out_11),
    .imageDataIn(video_data), .controlIn(video_ctrl), .controlIn_2(video_section_1_controlin_2),
    .imageDataIn_2(video_section_1_imagedatain_2));
  video_section video_section_2 (
    .chipID(video_section_1_out_18), .ballX(video_section_1_out_19), .ballY(video_section_1_out_20),
    .leftbatY(video_section_1_out_21), .rightbatY(video_section_1_out_22), .out_18(video_section_2_out_18),
    .out_19(video_section_2_out_19), .out_20(video_section_2_out_20), .out_21(video_section_2_out_21),
    .out_22(video_section_2_out_22), .out_13(video_section_2_out_13), .out_8(video_section_2_out_8),
    .out_14(video_section_2_out_14), .out_9(video_section_2_out_9), .out_15(video_section_2_out_15),
    .out_10(video_section_2_out_10), .out_16(video_section_2_out_16), .out_11(video_section_2_out_11),
    .imageDataIn(video_section_1_imagedatain_2), .controlIn(video_section_1_controlin_2),
    .controlIn_2(video_section_2_controlin_2), .imageDataIn_2(video_section_2_imagedatain_2));
  video_section video_section_3 (
    .chipID(video_section_2_out_18), .ballX(video_section_2_out_19), .ballY(video_section_2_out_20),
    .leftbatY(video_section_2_out_21), .rightbatY(video_section_2_out_22), .out_18(video_section_3_out_18),
    .out_19(video_section_3_out_19), .out_20(video_section_3_out_20), .out_21(video_section_3_out_21),
    .out_22(video_section_3_out_22), .out_13(video_section_3_out_13), .out_8(video_section_3_out_8),
    .out_14(video_section_3_out_14), .out_9(video_section_3_out_9), .out_15(video_section_3_out_15),
    .out_10(video_section_3_out_10), .out_16(video_section_3_out_16), .out_11(video_section_3_out_11),
    .imageDataIn(video_section_2_imagedatain_2), .controlIn(video_section_2_controlin_2),
    .controlIn_2(video_section_3_controlin_2), .imageDataIn_2(video_section_3_imagedatain_2));
  video_section video_section_4 (
    .chipID(video_section_3_out_18), .ballX(video_section_3_out_19), .ballY(video_section_3_out_20),
    .leftbatY(video_section_3_out_21), .rightbatY(video_section_3_out_22), .out_13(video_section_4_out_13),
    .out_8(video_section_4_out_8), .out_14(video_section_4_out_14), .out_9(video_section_4_out_9),
    .out_15(video_section_4_out_15), .out_10(video_section_4_out_10), .out_16(video_section_4_out_16),
    .out_11(video_section_4_out_11), .imageDataIn(video_section_3_imagedatain_2),
    .controlIn(video_section_3_controlin_2));  // open: out_18, out_19, out_20, out_21, out_22, controlIn_2, imageDataIn_2
  Hex_Digit_Display hex_digit_display_3 (.value(ten_2_out_2));  // open: dp
  Hex_Digit_Display hex_digit_display_4 (.value(ten_2_out_3));  // open: dp
  ten ten_2 (.in_1(bs), .out_2(ten_2_out_2), .out_3(ten_2_out_3));
  Comparator comparator_1 (.a(as), .b(8'h5), .eq(win));  // open: gt, lt
  Comparator comparator_2 (.a(bs), .b(8'h5), .eq(loose));  // open: gt, lt
  S_R_Flip_Flop s_r_ff_1 (.Qn(real_ns), .preset(start));  // open: S, clk, R, Q, reset, en
  Counter counter_1 (.Q(counter_1_q), .clk(and_2_out));  // open: load, D, count, carry, clr
  and and_2 (and_2_out, clk, ~counter_1_q[5]);  // AND_Gate
  Clock clock_3 (.out(clk));
  or or_2 (not_started, real_ns, ee);
  not not_1 (rst, counter_1_q[5]);
  or or_3 (gameOver, win, loose);
  or or_4 (or_4_out, vx[15], start);
  or or_5 (en_video, not_started, gameOver);
  Clock clock_4 (.out(clock_4_out));
  not not_2 (not_2_out, en_video);
  Multiplexer #(.width(2), .enable("false")) multiplexer_1 (
    .in0(2'b10), .in1(2'b01), .out(multiplexer_1_out), .sel(win));
  Register #(.width(16)) register_1 (.D(bx), .en(ld), .Q(register_1_q), .clk(ld));  // open: clr
  Counter #(.width(2), .max('h3), .ongoal("stay")) counter_2 (
    .Q({ld, counter_2_q[0]}), .clk(clk), .clr(or_4_out));  // open: load, D, count, carry
  and and_3 (video_clk, en_video, clock_4_out);
  Counter #(.width(2), .max('h3), .ongoal("stay")) counter_3 (
    .carry(counter_3_carry), .clk(clock_4_out), .clr(not_2_out));  // open: load, D, count, Q
  not not_3 (not_3_out, counter_3_carry);
  Multiplexer #(.width(2), .enable("false")) multiplexer_2 (
    .in0(2'b00), .in1(multiplexer_1_out), .out(multiplexer_2_out), .sel(gameOver));
  Register #(.width(16)) register_2 (.D(by), .en(ld), .Q(register_2_q), .clk(ld));  // open: clr
  and and_4 (and_4_out, ~rst, ~en_video, clk);  // AND_Gate
  video_player video_player_1 (
    .enable(en_video), .clock(video_clk), .data(video_data), .control(video_ctrl), .set(not_3_out),
    .num(multiplexer_3_out));
  Multiplexer #(.width(2), .enable("false")) multiplexer_3 (
    .in0(multiplexer_2_out), .in1(2'b11), .out(multiplexer_3_out), .sel(ee));
  ai ai_1 (
    .reset(or_4_out), .clock(and_4_out), .bx(register_1_q), .by(register_2_q), .vx(register_3_q),
    .vy(register_4_q), .vy_2(ry));
  secret secret_1 (.a(la), .b(lb), .x(lx), .y(ly), .reset(or_6_out), .result(ee));
  or or_6 (or_6_out, start, real_ns);
  Register #(.width(16)) register_3 (.D(vx), .en(ld), .Q(register_3_q), .clk(ld));  // open: clr
  Register #(.width(16)) register_4 (.D(vy), .en(ld), .Q(register_4_q), .clk(ld));  // open: clr

  // Notes on the sheet:
  //   Real gamepad
  //   Reset on power on
  //   Game over detection
  //   AI
  //   Video Player
endmodule

module video_chip (
  input  [7:0] controlIn,
  input  [31:0] imageDataIn,
  input  [4:0] chipID,
  input  [4:0] ballX,
  input  [4:0] ballY,
  input  [4:0] leftbatY,
  input  [4:0] rightbatY,
  output [7:0] controlOut,
  output [31:0] imageDataOut,
  output [31:0] out,
  output [4:0] out_11,
  output [4:0] out_12,
  output [4:0] out_13,
  output [4:0] out_14,
  output [4:0] out_15
);

  wire comparator_1_eq;
  wire [31:0] or_1_out, or_2_out, register_1_q, register_2_q, shifter_1_out, shifter_2_out,
       super_decoder_32_1_out, super_decoder_32_2_out, super_decoder_32_3_out;

  Adder #(.width(5)) adder_1 (.a(5'b00001), .b(chipID), .out(out_11));  // open: cin, cout
  Register #(.width(32), .trigger("high")) register_1 (
    .D(imageDataIn), .en(controlIn[5]), .Q(register_1_q), .clk(comparator_1_eq));  // open: clr
  Comparator #(.width(5), .mode("unsigned")) comparator_1 (
    .a(controlIn[4:0]), .b(chipID), .eq(comparator_1_eq));  // open: gt, lt
  super_decoder_32 super_decoder_32_1 (.data(ballY), .out(super_decoder_32_1_out), .A(ballX), .B(chipID));
  super_decoder_32 super_decoder_32_2 (.data(leftbatY), .out(super_decoder_32_2_out), .A(chipID), .B(5'b00011));
  assign or_1_out = super_decoder_32_2_out | super_decoder_32_3_out;  // OR_Gate or_1, 32 bits wide
  super_decoder_32 super_decoder_32_3 (.data(rightbatY), .out(super_decoder_32_3_out), .A(chipID), .B(5'b11100));
  Register #(.width(32), .trigger("high")) register_2 (
    .D(register_1_q), .en(controlIn[6]), .Q(register_2_q), .clk(controlIn[6]));  // open: clr
  Shifter #(.width(32)) shifter_1 (.in(or_1_out), .\dist (5'b00010), .out(shifter_1_out));
  Shifter #(.width(32)) shifter_2 (.in(or_1_out), .\dist (5'b00001), .out(shifter_2_out));
  assign or_2_out = super_decoder_32_1_out | or_1_out | shifter_1_out | shifter_2_out;  // OR_Gate or_2, 32 bits wide
  Multiplexer #(.width(32), .enable("false")) multiplexer_1 (
    .in0(or_2_out), .in1(register_2_q), .out(out), .sel(controlIn[7]));

  assign controlOut = controlIn;
  assign imageDataOut = imageDataIn;
  assign out_12 = ballX;
  assign out_13 = ballY;
  assign out_14 = leftbatY;
  assign out_15 = rightbatY;

  // Other names for the same wires on the sheet: chip_id[4:0] = chipID; enable_video = controlIn[7]
endmodule

module super_decoder_32 (
  input  [4:0] data,
  input  [4:0] A,
  input  [4:0] B,
  output [31:0] out
);

  wire comparator_1_eq;

  Comparator #(.width(5)) comparator_1 (.a(A), .b(B), .eq(comparator_1_eq));  // open: gt, lt
  Decoder #(.select(5), .disabled(0)) decoder_1 (
    .out0(out[0]), .out1(out[1]), .out2(out[2]), .out3(out[3]), .out4(out[4]), .out5(out[5]), .out6(out[6]),
    .out7(out[7]), .out8(out[8]), .out9(out[9]), .out10(out[10]), .out11(out[11]), .out12(out[12]),
    .out13(out[13]), .out14(out[14]), .out15(out[15]), .out16(out[16]), .out17(out[17]), .out18(out[18]),
    .out19(out[19]), .out20(out[20]), .out21(out[21]), .out22(out[22]), .out23(out[23]), .out24(out[24]),
    .out25(out[25]), .out26(out[26]), .out27(out[27]), .out28(out[28]), .out29(out[29]), .out30(out[30]),
    .out31(out[31]), .sel(data), .en(comparator_1_eq));
endmodule

module video_section (
  input  [7:0] controlIn,
  input  [31:0] imageDataIn,
  input  [4:0] chipID,
  input  [4:0] ballX,
  input  [4:0] ballY,
  input  [4:0] leftbatY,
  input  [4:0] rightbatY,
  output [31:0] out_8,
  output [31:0] out_9,
  output [31:0] out_10,
  output [31:0] out_11,
  output [7:0] controlIn_2,
  output [31:0] out_13,
  output [31:0] out_14,
  output [31:0] out_15,
  output [31:0] out_16,
  output [31:0] imageDataIn_2,
  output [4:0] out_18,
  output [4:0] out_19,
  output [4:0] out_20,
  output [4:0] out_21,
  output [4:0] out_22
);

  wire [4:0] video_chip_1_out_11, video_chip_1_out_12, video_chip_1_out_13, video_chip_1_out_14,
       video_chip_1_out_15, video_chip_2_out_11, video_chip_2_out_12, video_chip_2_out_13,
       video_chip_2_out_14, video_chip_2_out_15, video_chip_3_out_11, video_chip_3_out_12,
       video_chip_3_out_13, video_chip_3_out_14, video_chip_3_out_15, video_chip_4_out_11,
       video_chip_4_out_12, video_chip_4_out_13, video_chip_4_out_14, video_chip_4_out_15,
       video_chip_5_out_11, video_chip_5_out_12, video_chip_5_out_13, video_chip_5_out_14,
       video_chip_5_out_15, video_chip_6_out_11, video_chip_6_out_12, video_chip_6_out_13,
       video_chip_6_out_14, video_chip_6_out_15, video_chip_8_out_11, video_chip_8_out_12,
       video_chip_8_out_13, video_chip_8_out_14, video_chip_8_out_15;
  wire [7:0] video_chip_1_controlout, video_chip_2_controlout, video_chip_3_controlout,
       video_chip_4_controlout, video_chip_5_controlout, video_chip_6_controlout, video_chip_8_controlout;
  wire [31:0] video_chip_1_imagedataout, video_chip_2_imagedataout, video_chip_3_imagedataout,
       video_chip_4_imagedataout, video_chip_5_imagedataout, video_chip_6_imagedataout,
       video_chip_8_imagedataout;

  video_chip video_chip_1 (
    .out_11(video_chip_1_out_11), .out_12(video_chip_1_out_12), .ballX(video_chip_2_out_12),
    .out_13(video_chip_1_out_13), .ballY(video_chip_2_out_13), .out_14(video_chip_1_out_14),
    .leftbatY(video_chip_2_out_14), .out_15(video_chip_1_out_15), .rightbatY(video_chip_2_out_15),
    .out(out_8), .chipID(video_chip_2_out_11), .imageDataIn(video_chip_2_imagedataout),
    .controlIn(video_chip_2_controlout), .controlOut(video_chip_1_controlout),
    .imageDataOut(video_chip_1_imagedataout));
  video_chip video_chip_2 (
    .out_11(video_chip_2_out_11), .out_12(video_chip_2_out_12), .ballX(ballX), .out_13(video_chip_2_out_13),
    .ballY(ballY), .out_14(video_chip_2_out_14), .leftbatY(leftbatY), .out_15(video_chip_2_out_15),
    .rightbatY(rightbatY), .out(out_13), .chipID(chipID), .imageDataIn(imageDataIn), .controlIn(controlIn),
    .controlOut(video_chip_2_controlout), .imageDataOut(video_chip_2_imagedataout));
  video_chip video_chip_3 (
    .out_11(video_chip_3_out_11), .out_12(video_chip_3_out_12), .ballX(video_chip_4_out_12),
    .out_13(video_chip_3_out_13), .ballY(video_chip_4_out_13), .out_14(video_chip_3_out_14),
    .leftbatY(video_chip_4_out_14), .out_15(video_chip_3_out_15), .rightbatY(video_chip_4_out_15),
    .out(out_9), .chipID(video_chip_4_out_11), .imageDataIn(video_chip_4_imagedataout),
    .controlIn(video_chip_4_controlout), .controlOut(video_chip_3_controlout),
    .imageDataOut(video_chip_3_imagedataout));
  video_chip video_chip_4 (
    .out_11(video_chip_4_out_11), .out_12(video_chip_4_out_12), .ballX(video_chip_1_out_12),
    .out_13(video_chip_4_out_13), .ballY(video_chip_1_out_13), .out_14(video_chip_4_out_14),
    .leftbatY(video_chip_1_out_14), .out_15(video_chip_4_out_15), .rightbatY(video_chip_1_out_15),
    .out(out_14), .chipID(video_chip_1_out_11), .imageDataIn(video_chip_1_imagedataout),
    .controlIn(video_chip_1_controlout), .controlOut(video_chip_4_controlout),
    .imageDataOut(video_chip_4_imagedataout));
  video_chip video_chip_5 (
    .out_11(video_chip_5_out_11), .out_12(video_chip_5_out_12), .ballX(video_chip_6_out_12),
    .out_13(video_chip_5_out_13), .ballY(video_chip_6_out_13), .out_14(video_chip_5_out_14),
    .leftbatY(video_chip_6_out_14), .out_15(video_chip_5_out_15), .rightbatY(video_chip_6_out_15),
    .out(out_10), .chipID(video_chip_6_out_11), .imageDataIn(video_chip_6_imagedataout),
    .controlIn(video_chip_6_controlout), .controlOut(video_chip_5_controlout),
    .imageDataOut(video_chip_5_imagedataout));
  video_chip video_chip_6 (
    .out_11(video_chip_6_out_11), .out_12(video_chip_6_out_12), .ballX(video_chip_3_out_12),
    .out_13(video_chip_6_out_13), .ballY(video_chip_3_out_13), .out_14(video_chip_6_out_14),
    .leftbatY(video_chip_3_out_14), .out_15(video_chip_6_out_15), .rightbatY(video_chip_3_out_15),
    .out(out_15), .chipID(video_chip_3_out_11), .imageDataIn(video_chip_3_imagedataout),
    .controlIn(video_chip_3_controlout), .controlOut(video_chip_6_controlout),
    .imageDataOut(video_chip_6_imagedataout));
  video_chip video_chip_7 (
    .out_11(out_18), .out_12(out_19), .ballX(video_chip_8_out_12), .out_13(out_20),
    .ballY(video_chip_8_out_13), .out_14(out_21), .leftbatY(video_chip_8_out_14), .out_15(out_22),
    .rightbatY(video_chip_8_out_15), .out(out_11), .chipID(video_chip_8_out_11),
    .imageDataIn(video_chip_8_imagedataout), .controlIn(video_chip_8_controlout), .controlOut(controlIn_2),
    .imageDataOut(imageDataIn_2));
  video_chip video_chip_8 (
    .out_11(video_chip_8_out_11), .out_12(video_chip_8_out_12), .ballX(video_chip_5_out_12),
    .out_13(video_chip_8_out_13), .ballY(video_chip_5_out_13), .out_14(video_chip_8_out_14),
    .leftbatY(video_chip_5_out_14), .out_15(video_chip_8_out_15), .rightbatY(video_chip_5_out_15),
    .out(out_16), .chipID(video_chip_5_out_11), .imageDataIn(video_chip_5_imagedataout),
    .controlIn(video_chip_5_controlout), .controlOut(video_chip_8_controlout),
    .imageDataOut(video_chip_8_imagedataout));
endmodule

module inrange (
  input  [4:0] yball,
  input  [4:0] ybat,
  output out_3
);

  wire comparator_1_eq, comparator_2_eq, comparator_3_eq;
  wire [4:0] adder_1_out, adder_2_out;

  Adder #(.width(5)) adder_1 (.a(ybat), .b(5'b00001), .out(adder_1_out));  // open: cin, cout
  Adder #(.width(5)) adder_2 (.a(ybat), .b(5'b00010), .out(adder_2_out));  // open: cin, cout
  Comparator #(.width(5)) comparator_1 (.a(yball), .b(ybat), .eq(comparator_1_eq));  // open: gt, lt
  Comparator #(.width(5)) comparator_2 (.a(yball), .b(adder_1_out), .eq(comparator_2_eq));  // open: gt, lt
  Comparator #(.width(5)) comparator_3 (.a(yball), .b(adder_2_out), .eq(comparator_3_eq));  // open: gt, lt
  or or_1 (out_3, comparator_1_eq, comparator_2_eq, comparator_3_eq);
endmodule

module kinematic (
  input  clock,
  input  reset,
  input  [4:0] leftYin,
  input  [4:0] rightYin,
  output [4:0] zero,
  output [4:0] ballx,
  output [4:0] bally,
  output [4:0] leftYout,
  output [4:0] rightYout,
  output [7:0] scoreA,
  output [7:0] scoreB,
  output [15:0] bx,
  output [15:0] vx,
  output [15:0] by,
  output [15:0] vy
);

  wire adder_7_cout, adder_8_cout, and_1_out, and_4_out, Bcontact, counter_1_carry, hit, hitA, hitB,
       inrange_1_out_3, inrange_2_out_3, LBcontact, multiplexer_6_out, not_1_out, not_2_out, not_3_out,
       not_4_out, not_5_out, not_6_out, not_7_out, or_1_out, or_2_out, or_4_out, or_5_out, or_7_out,
       posReset, RBcontact, s_r_ff_1_q, vxneg, xor_1_out, xor_2_out, xor_3_out, xor_4_out, xrefl, yrefl;
  wire [1:0] comparator_1_gt;
  wire [4:0] adder_12_out, adder_13_out, register_3_q;
  wire [5:0] random_2_out;
  wire [7:0] adder_9_out, adder_10_out, adder_11_out, angle, angle_calculator_1_angle,
       angle_calculator_2_angle, bit_extender_1_out, modified_angle, multiplexer_4_out, multiplexer_5_out,
       multiplexer_7_out, negator_1_out, random_1_out, real_angle;
  wire [14:0] adder_3_out, adder_4_out;
  wire [15:0] adder_1_out, adder_2_out, adder_5_out, adder_6_out, multiplexer_1_out, multiplexer_2_out,
       multiplexer_3_out;

  Adder #(.width(16)) adder_1 (.a({bx[15], ballx, bx[9:0]}), .b(vx), .out(adder_1_out));  // open: cin, cout
  Multiplexer #(.width(16), .enable("false")) multiplexer_1 (
    .in0(16'he80), .in1(16'h7180), .out(multiplexer_1_out), .sel(vxneg));
  not not_1 (not_1_out, xrefl);
  not not_2 (not_2_out, Bcontact);
  Adder #(.width(16)) adder_2 (.a({by[15], bally, by[9:0]}), .b(vy), .out(adder_2_out));  // open: cin, cout
  not not_3 (not_3_out, xrefl);
  Multiplexer #(.width(16), .enable("false")) multiplexer_2 (
    .in0(adder_1_out), .in1(multiplexer_1_out), .out(multiplexer_2_out), .sel(posReset));
  and and_1 (and_1_out, not_1_out, not_2_out);
  or or_1 (or_1_out, and_1_out, posReset);
  Multiplexer #(.width(16), .enable("false")) multiplexer_3 (
    .in0(adder_2_out), .in1(16'h4000), .out(multiplexer_3_out), .sel(posReset));
  or or_2 (or_2_out, not_3_out, posReset);
  S_R_Flip_Flop #(.trigger("falling")) s_r_ff_1 (
    .S(1'b0), .clk(clock), .R(1'b1), .Q(s_r_ff_1_q), .preset(hit), .en(1'b1));  // open: Qn, reset
  Register #(.width(16), .trigger("falling")) xreg (
    .D(multiplexer_2_out), .en(or_1_out), .Q({bx[15], ballx, bx[9:0]}), .clk(clock));  // open: clr
  Register #(.width(16), .trigger("falling")) yreg (
    .D(multiplexer_3_out), .en(or_2_out), .Q({by[15], bally, by[9:0]}), .clk(clock));  // open: clr
  or or_3 (posReset, reset, s_r_ff_1_q);
  // Probe on {bx[15], ballx, bx[9:0]}
  Adder #(.width(16)) adder_3 (.a({bx[15], ballx, bx[9:0]}), .b(vx), .out({xrefl, adder_3_out}));  // open: cin, cout
  Adder #(.width(16)) adder_4 (.a({by[15], bally, by[9:0]}), .b(vy), .out({yrefl, adder_4_out}));  // open: cin, cout
  angle_calculator angle_calculator_1 (
    .ball({by[15], bally, by[9:0]}), .bat(leftYin), .angle(angle_calculator_1_angle));
  angle_calculator angle_calculator_2 (
    .ball({by[15], bally, by[9:0]}), .bat(rightYout), .angle(angle_calculator_2_angle));
  Random random_1 (.clk(hit), .next(1'b1), .out(random_1_out));  // open: clr
  // Probe on adder_5_out
  Adder #(.width(16)) adder_5 (.a({bx[15], ballx, bx[9:0]}), .b(16'hf200), .out(adder_5_out));  // open: cin, cout
  Adder #(.width(16)) adder_6 (.a({bx[15], ballx, bx[9:0]}), .b(16'h8e00), .out(adder_6_out));  // open: cin, cout
  Multiplexer #(.width(8), .enable("false")) multiplexer_4 (
    .in0(angle_calculator_1_angle), .in1(angle_calculator_2_angle), .out(multiplexer_4_out), .sel(RBcontact));
  not not_4 (not_4_out, hitB);
  Adder #(.width(16)) adder_7 (.a(adder_5_out), .b(vx), .cout(adder_7_cout));  // open: out, cin
  inrange inrange_1 (.yball(bally), .ybat(leftYin), .out_3(inrange_1_out_3));
  Adder #(.width(16)) adder_8 (.a(adder_6_out), .b(vx), .cout(adder_8_cout));  // open: out, cin
  inrange inrange_2 (.yball(bally), .ybat(rightYout), .out_3(inrange_2_out_3));
  Multiplexer #(.width(8), .enable("false")) multiplexer_5 (
    .in0(angle), .in1(multiplexer_4_out), .out(multiplexer_5_out), .sel(Bcontact));
  Multiplexer #(.enable("false")) multiplexer_6 (.in0(not_5_out), .in1(not_4_out), .out(multiplexer_6_out), .sel(hit));
  xor xor_1 (xor_1_out, adder_7_cout, vxneg);
  xor xor_2 (xor_2_out, adder_8_cout, vxneg);
  Multiplexer #(.width(8), .enable("false")) multiplexer_7 (
    .in0(multiplexer_5_out), .in1(random_1_out), .out(multiplexer_7_out), .sel(posReset));
  or or_4 (or_4_out, reset, Bcontact, hit, xrefl);
  and and_2 (LBcontact, xor_1_out, inrange_1_out_3);
  and and_3 (RBcontact, xor_2_out, inrange_2_out_3);
  Multiplexer #(.width(8), .enable("false")) multiplexer_8 (
    .in0(real_angle), .in1(negator_1_out), .out(angle), .sel(yrefl));
  Negator negator_1 (.in(real_angle), .out(negator_1_out));
  Register u_angle (.D(multiplexer_7_out), .en(or_5_out), .Q(real_angle), .clk(clock));  // open: clr
  or or_5 (or_5_out, yrefl, Bcontact, posReset);
  not not_5 (not_5_out, vxneg);
  or or_6 (Bcontact, LBcontact, RBcontact);
  Register #(.width(1)) u_vxneg (.D(multiplexer_6_out), .en(or_4_out), .Q(vxneg), .clk(clock), .clr(reset));
  Random #(.width(6), .trigger("falling")) random_2 (.clk(vxneg), .next(1'b1), .out(random_2_out));  // open: clr
  assign bit_extender_1_out = {{2{random_2_out[5]}}, random_2_out};  // Bit_Extender bit_extender_1
  // Probe on vy
  velocity_calculator velocity_calculator_1 (.angle(modified_angle), .xdir(vxneg), .vy(vy), .vx(vx));
  // Probe on vx
  Adder adder_9 (.a(scoreA), .b(8'h1), .out(adder_9_out));  // open: cin, cout
  Adder adder_10 (.a(scoreB), .b(8'h1), .out(adder_10_out));  // open: cin, cout
  Adder adder_11 (.a(bit_extender_1_out), .b(real_angle), .out(adder_11_out));  // open: cin, cout
  xor xor_3 (xor_3_out, real_angle[7], bit_extender_1_out[7]);
  xor xor_4 (xor_4_out, real_angle[7], adder_11_out[7]);
  Register register_1 (.D(adder_9_out), .en(hitA), .Q(scoreA), .clk(clock), .clr(reset));
  Register register_2 (.D(adder_10_out), .en(hitB), .Q(scoreB), .clk(clock), .clr(reset));
  or or_7 (or_7_out, xor_3_out, ~xor_4_out);  // OR_Gate
  and and_4 (and_4_out, or_7_out, ballx[4]);
  Multiplexer #(.width(8), .enable("false")) multiplexer_9 (
    .in0(real_angle), .in1(adder_11_out), .out(modified_angle), .sel(and_4_out));
  Counter #(.width(2), .max('h3)) counter_1 (
    .count(clock), .carry(counter_1_carry), .clk(clock));  // open: load, D, Q, clr
  not not_6 (not_6_out, Bcontact);
  Register #(.width(5)) register_3 (.D(rightYout), .en(1'b1), .Q(register_3_q), .clk(counter_1_carry));  // open: clr
  not not_7 (not_7_out, vxneg);
  Adder #(.width(5)) adder_12 (.a(5'b00001), .b(register_3_q), .out(adder_12_out));  // open: cin, cout
  Adder #(.width(5)) adder_13 (.a({5{1'b1}}), .b(register_3_q), .out(adder_13_out));  // open: cin, cout
  Comparator #(.width(5), .mode("unsigned")) comparator_1 (
    .a(register_3_q), .b(rightYin), .gt(comparator_1_gt[0]), .eq(comparator_1_gt[1]));  // open: lt
  and and_5 (hitB, xrefl, not_6_out, vxneg);
  and and_6 (hitA, xrefl, not_6_out, not_7_out);
  or or_8 (hit, hitB, hitA);
  Multiplexer #(.select(2), .width(5), .enable("false")) multiplexer_10 (
    .in0(adder_12_out), .in1(adder_13_out), .in2(register_3_q), .in3(register_3_q), .out(rightYout),
    .sel(comparator_1_gt));

  assign bx[14:10] = ballx;
  assign by[14:10] = bally;
  assign leftYout = leftYin;
  assign zero = {5{1'b0}};

  // Other names for the same wires on the sheet: clk = clock; longVX[15:0] = vx; longVY[15:0] = vy;
  //   vyneg = real_angle[7]; scA[7:0] = scoreA; scB[7:0] = scoreB; xreg[15:0] = {bx[15], ballx, bx[9:0]};
  //   yreg[15:0] = {by[15], bally, by[9:0]}

  // Notes on the sheet:
  //   IO
  //   Ball position calculation
  //   Ball postion reset
  //   Ball velocity calculation
  //   Ball reflection detection
  //   Bat contact detection
  //   Score
  //   To force bot loose sometimes
  //   Angle randomization
  //   Right bat coordinate calulation
  //   Adds smooth movement
  //   Hit detection
endmodule

module ten (
  input  [7:0] in_1,
  output [3:0] out_2,
  output [3:0] out_3
);

  wire [7:4] divider_1_out, divider_1_rem;

  // Probe on in_1
  Divider divider_1 (.a(in_1), .b(8'ha), .out({divider_1_out, out_2}), .rem({divider_1_rem, out_3}));  // open: upper
  // Probe on out_2
  // Probe on out_3
endmodule

module iodevice (
  input  [7:0] rd,
  input  [7:0] addrIn,
  input  [7:0] memRdIn,
  input  [7:0] memWrIn,
  input  doWriteIn,
  input  [7:0] neededAddr,
  output [7:0] wr,
  output doWrite,
  output [7:0] addrOut,
  output [7:0] memRdOut,
  output [7:0] memWrOut,
  output doWriteOut
);

  wire comparator_1_eq;

  Multiplexer #(.width(8), .enable("false")) multiplexer_1 (
    .in0(memRdIn), .in1(rd), .out(memRdOut), .sel(comparator_1_eq));
  Comparator #(.mode("unsigned")) comparator_1 (.a(addrIn), .b(neededAddr), .eq(comparator_1_eq));  // open: gt, lt
  and and_1 (doWrite, comparator_1_eq, doWriteIn);

  assign addrOut = addrIn;
  assign doWriteOut = doWriteIn;
  assign memWrOut = memWrIn;
  assign wr = memWrIn;
endmodule

module video_player (
  input  set,
  input  enable,
  input  clock,
  input  [1:0] num,
  output [31:0] data,
  output [7:0] control
);

  wire comparator_1_eq, not_1_out, or_1_out;
  wire [23:0] adder_1_out, end_addr, multiplexer_1_out, start_addr;
  wire [23:5] register_1_q;

  Multiplexer #(.width(24), .enable("false")) multiplexer_1 (
    .in0(adder_1_out), .in1(start_addr), .out(multiplexer_1_out), .sel(set));
  Comparator #(.width(24), .mode("unsigned")) comparator_1 (
    .a({register_1_q, control[4:0]}), .b(end_addr), .eq(comparator_1_eq));  // open: gt, lt
  not not_1 (not_1_out, comparator_1_eq);
  and and_1 (control[5], enable, clock);
  Adder #(.width(24)) adder_1 (
    .a({24{1'b0}}), .b({register_1_q, control[4:0]}), .out(adder_1_out), .cin(not_1_out));  // open: cout
  Register #(.width(24)) register_1 (
    .D(multiplexer_1_out), .en(control[5]), .Q({register_1_q, control[4:0]}), .clk(control[5]));  // open: clr
  Multiplexer #(.select(2), .width(24), .enable("false")) multiplexer_2 (
    .in0({24{1'b0}}), .in1(24'h6a0), .in2(24'h8c0), .in3(24'hae0), .out(start_addr), .sel(num));
  Comparator #(.width(5), .mode("unsigned")) comparator_2 (
    .a(control[4:0]), .b({5{1'b1}}), .eq(control[6]));  // open: gt, lt
  Multiplexer #(.select(2), .width(24), .enable("false")) multiplexer_3 (
    .in0(24'h69f), .in1(24'h8bf), .in2(24'hadf), .in3(24'h11c9f), .out(end_addr), .sel(num));
  ROM #(.addrWidth(24), .dataWidth(32)) rom_1 (.addr({register_1_q, control[4:0]}), .data(data), .sel(1'b1));
  S_R_Flip_Flop s_r_ff_1 (.Q(control[7]), .preset(control[6]), .reset(or_1_out));  // open: S, clk, R, Qn, en
  or or_1 (or_1_out, ~enable, set);  // OR_Gate

  // Notes on the sheet:
  //   contents of rom_1 (hex, n*v repeats v):
  //   ebff80ff ebffafff e83f8fff eb9fffff ebef80ff ffffa7ff e07f88ff ef1fffff ebdf80ff ebcfb6ff ebffb6ff
  //   ffffffff fe0f86ff f9ffb6ff f77fb0ff ef7fffff e00f80ff ffffb6ff fc0fb6ff f3ffffff efff80ff e8ffefff
  //   effff7ff f3ff80ff fc0fffff ffffbfff e00f80ff ffffbfff eeefffff eeef86ff f7dfb6ff f83fb0ff ebff80ff
  //   ebffafff e83f8fff eb9fffff ebef80ff ffffa7ff e07f88ff ef1fffff ebdf80ff ebcfb6ff ebffb6ff ffffffff
  //   fe0f86ff f9ffb6ff f77fb0ff ef7fffff e00f80ff ffffb6ff fc0fb6ff f3ffffff efff80ff e8ffefff effff7ff
  //   f3ff80ff fc0fffff ffffbfff e00f80ff ffffbfff eeefffff eeef86ff f7dfb6ff f83fb0ff ebff80ff ebffafff
  //   e83f8fff eb9fffff ebef80ff ffffa7ff e07f88ff ef1fffff ebdf80ff ebcfb6ff ebffb6ff ffffffff fe0f86ff
  //   f9ffb6ff f77fb0ff ef7fffff e00f80ff ffffb6ff fc0fb6ff f3ffffff efff80ff e8ffefff effff7ff f3ff80ff
  //   fc0fffff ffffbfff e00f80ff ffffbfff eeefffff eeef86ff f7dfb6ff f83fb0ff ebff80ff ebffafff e83f8fff
  //   eb9fffff ebef80ff ffffa7ff e07f88ff ef1fffff ebdf80ff ebcfb6ff ebffb6ff ffffffff fe0f86ff f9ffb6ff
  //   f77fb0ff ef7fffff e00f80ff ffffb6ff fc0fb6ff f3ffffff efff80ff e8ffefff effff7ff f3ff80ff fc0fffff
  //   ffffbfff e00f80ff ffffbfff eeefffff eeef86ff f7dfb6ff f83fb0ff affe03ff affebfff a0fe3fff ae7fffff
  //   afbe03ff fffe9fff 81fe23ff bc7fffff af7e03ff af3edbff affedbff ffffffff f83e1bff e7fedbff ddfec3ff
  //   bdffffff 803e03ff fffedbff f03edbff cfffffff bffe03ff a3ffbfff bfffdfff cffe03ff f03fffff fffeffff
  //   803e03ff fffeffff bbbfffff bbbe1bff df7edbff e0fec3ff bff80fff bffaffff 83f8ffff b9fffffc bef80ffd
  //   fffa7ffd 7f88fff f1fffffc bdf80ffd bcfb6ffc bffb6fff fffffffc e0f86ffd 9ffb6ffd 77fb0fff f7fffffc
  //   f80ffd fffb6ffd c0fb6fff 3ffffffd fff80ffc 8ffefffd ffff7fff 3ff80ffe c0fffffd fffbfffe f80fff
  //   fffbfffc eeffffff eef86fff 7dfb6fff 83fb0fff ffe03fff ffebffff fe3ffff e7fffff0 fbe03ff6 ffe9fff6
  //   1fe23fff c7fffff0 f7e03ff5 f3edbff1 ffedbfff fffffff0 83e1bff6 7fedbff6 dfec3fff dffffff0 3e03ff7
  //   ffedbff7 3edbfff fffffff7 ffe03ff0 3ffbfff7 fffdffff ffe03ff8 3fffff6 ffeffff8 3e03fff ffeffff0
  //   bbffffff bbe1bfff f7edbfff fec3fff ff80ffff ffafffff 3f8fffff 9fffffc3 ef80ffdb ffa7ffd8 7f88ffff
  //   1fffffc0 df80ffd7 cfb6ffc7 ffb6ffff ffffffc0 f86ffdb ffb6ffdb 7fb0ffff 7fffffc0 f80ffdf ffb6ffdf
  //   fb6ffff ffffffdf ff80ffc0 ffefffdf fff7ffff ff80ffe0 fffffdb ffbfffe0 f80ffff ffbfffc0 efffffff
  //   ef86ffff dfb6ffff 3fb0ffff fe03ffff febfffff fe3fffff 7fffff0d be03ff6d fe9fff61 fe23ffff 7fffff01
  //   7e03ff5f 3edbff1f fedbffff ffffff01 3e1bff6d fedbff6d fec3ffff ffffff01 3e03ff7d fedbff7d 3edbffff
  //   ffffff7d fe03ff01 ffbfff7d ffdfffff fe03ff81 3fffff6f feffff81 3e03ffff feffff01 bffffffd be1bfffd
  //   7edbffff fec3ffff f80fffff faffffff f8ffffff fffffc37 f80ffdb6 fa7ffd86 f88ffffe fffffc07 f80ffd7e
  //   fb6ffc7f fb6ffffe fffffc07 f86ffdb7 fb6ffdb6 fb0fffff fffffc07 f80ffdf6 fb6ffdf7 fb6fffff fffffdf6
  //   f80ffc07 fefffdf6 ff7fffff f80ffe06 fffffdbf fbfffe06 f80ffffe fbfffc06 fffffff7 f86ffff7 fb6fffff
  //   fb0fffff e03fffff ebffffff e3ffffff fffff0df e03ff6db e9fff618 e23ffffb fffff01f e03ff5f8 edbff1ff
  //   edbffff8 fffff01f e1bff6dc edbff6db ec3ffffc fffff01f e03ff7d8 edbff7de edbfffff fffff7d8 e03ff01f
  //   fbfff7d8 fdfffffe e03ff819 fffff6ff effff818 e03ffffb effff01b ffffffdf e1bfffdf edbfffff ec3fffff
  //   80ffffff afffffff 8fffffff ffffc37f 80ffdb6f a7ffd860 88ffffef ffffc07f 80ffd7e0 b6ffc7fd b6ffffe0
  //   ffffc07f 86ffdb70 b6ffdb6d b0fffff0 ffffc07f 80ffdf60 b6ffdf7b b6fffffd ffffdf60 80ffc07f efffdf60
  //   f7fffff9 80ffe066 ffffdbff bfffe061 80ffffed bfffc06c ffffff7f 86ffff7f b6ffffff b0ffffff 3ffffff
  //   bfffffff 3fffffff ffff0dff 3ff6dbf 9fff6180 23ffffbf ffff01ff 3ff5f80 dbff1ff7 dbffff80 ffff01ff
  //   1bff6dc0 dbff6db7 c3ffffc0 ffff01ff 3ff7d80 dbff7def dbfffff7 ffff7d80 3ff01ff bfff7d80 dfffffe7
  //   3ff8198 ffff6fff ffff8186 3ffffb6 ffff01b0 fffffdff 1bfffdff dbffffff c3ffffff fffffff ffffffff
  //   ffffffff fffc37ff ffdb6ff 7ffd8603 8ffffeff fffc07ff ffd7e03 6ffc7fdf 6ffffe03 fffc07ff 6ffdb703
  //   6ffdb6df fffff03 fffc07ff ffdf603 6ffdf7bf 6fffffdf fffdf603 ffc07ff fffdf603 7fffff9f ffe0663
  //   fffdbfff fffe061b ffffedb fffc06c3 fffff7ff 6ffff7ff 6fffffff fffffff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
endmodule

module velocity_calculator (
  input  [7:0] angle,
  input  xdir,
  output [15:0] vy,
  output [15:0] vx
);

  wire comparator_1_eq;
  wire [6:0] multiplexer_2_out, negator_1_out;
  wire [7:0] multiplexer_1_out;
  wire [15:0] negator_2_out, negator_3_out, rom_1_data, rom_2_data;

  Comparator #(.mode("unsigned")) comparator_1 (.a(angle), .b(8'h80), .eq(comparator_1_eq));  // open: gt, lt
  // Probe on multiplexer_1_out
  Multiplexer #(.width(8), .enable("false")) multiplexer_1 (
    .in0(angle), .in1(8'h81), .out(multiplexer_1_out), .sel(comparator_1_eq));
  Negator #(.width(7)) negator_1 (.in(multiplexer_1_out[6:0]), .out(negator_1_out));
  Multiplexer #(.width(7), .enable("false")) multiplexer_2 (
    .in0(multiplexer_1_out[6:0]), .in1(negator_1_out), .out(multiplexer_2_out), .sel(multiplexer_1_out[7]));
  ROM #(.addrWidth(7), .dataWidth(16)) rom_1 (.addr(multiplexer_2_out), .data(rom_1_data), .sel(1'b1));
  ROM #(.addrWidth(7), .dataWidth(16)) rom_2 (.addr(multiplexer_2_out), .data(rom_2_data), .sel(1'b1));
  Negator #(.width(16)) negator_2 (.in(rom_1_data), .out(negator_2_out));
  Negator #(.width(16)) negator_3 (.in(rom_2_data), .out(negator_3_out));
  // Probe on vy
  Multiplexer #(.width(16), .enable("false")) multiplexer_3 (
    .in0(rom_1_data), .in1(negator_2_out), .out(vy), .sel(multiplexer_1_out[7]));
  // Probe on vx
  Multiplexer #(.width(16), .enable("false")) multiplexer_4 (
    .in0(rom_2_data), .in1(negator_3_out), .out(vx), .sel(xdir));

  // Notes on the sheet:
  //   sin - y
  //   cos - x
  //   contents of rom_1 (hex, n*v repeats v):
  //   0 1 2 3 4 5 5 6 7 8 9 a b c d e f f 10 11 12 13 14 15 16 17 18 19 19 1a 1b 1c 1d 1e 1f 20 21 21 22
  //   23 24 25 26 27 28 28 29 2a 2b 2c 2d 2e 2e 2f 30 31 32 33 33 34 35 36 37 38 38 39 3a 3b 3c 3c 3d 3e
  //   3f 40 40 41 42 43 44 44 45 46 47 47 48 49 4a 4a 4b 4c 4d 4d 4e 4f 50 50 51 52 52 53 54 54 55 56 56
  //   57 58 58 59 5a 5a 5b 5c 5c 5d 5e 5e 5f 5f 60 61 61 62 62 63 64 64 65
  //   contents of rom_2 (hex, n*v repeats v):
  //   13*80 9*7f 6*7e 5*7d 5*7c 4*7b 7a 7a 7a 4*79 78 78 78 77 77 77 76 76 76 75 75 74 74 74 73 73 72 72
  //   72 71 71 70 70 6f 6f 6f 6e 6e 6d 6d 6c 6c 6b 6b 6a 6a 69 69 68 68 67 67 66 65 65 64 64 63 63 62 61
  //   61 60 60 5f 5e 5e 5d 5c 5c 5b 5b 5a 59 59 58 57 57 56 55 55 54 53 53 52 51 50 50 4f
endmodule

module angle_calculator (
  input  [15:0] ball,
  input  [4:0] bat,
  output [7:0] angle
);

  wire [15:0] adder_1_out, subtractor_1_out;

  // Probe on adder_1_out
  Adder #(.width(16)) adder_1 (.a({1'b0, bat, {10{1'b0}}}), .b(16'h600), .out(adder_1_out));  // open: cin, cout
  Subtractor #(.width(16)) subtractor_1 (
    .a(ball), .b(adder_1_out), .out({subtractor_1_out[15:12], angle, subtractor_1_out[3:0]}));  // open: bin, bout
endmodule

module abs (
  input  [15:0] in,
  output [15:0] out,
  output was_done
);

  wire [15:0] negator_1_out;

  Negator #(.width(16)) negator_1 (.in(in), .out(negator_1_out));
  Multiplexer #(.width(16), .enable("false")) multiplexer_1 (.in0(in), .in1(negator_1_out), .out(out), .sel(in[15]));

  assign was_done = in[15];
endmodule

module ai (
  input  [15:0] bx,
  input  [15:0] by,
  input  [15:0] vx,
  input  [15:0] vy,
  input  reset,
  input  clock,
  output [4:0] vy_2
);

  wire abs_1_was_done, abs_2_was_done, and_1_out, and_2_out, and_3_out, doREAD, doWRITE, iodevice_1_dowrite,
       iodevice_1_dowriteout, iodevice_2_dowrite, iodevice_2_dowriteout, iodevice_3_dowrite,
       iodevice_3_dowriteout, iodevice_4_dowrite, iodevice_4_dowriteout, iodevice_5_dowrite,
       iodevice_5_dowriteout, iodevice_6_dowriteout, iodevice_7_dowriteout, iodevice_8_dowriteout,
       iodevice_9_dowriteout, iodevice_10_dowriteout, iodevice_11_dowriteout, iodevice_12_dowriteout,
       iodevice_13_dowriteout, iodevice_14_dowrite, mem, RAM, ROM, xor_1_out;
  wire [2:0] register_6_q;
  wire [6:0] iodevice_14_addrout;
  wire [7:0] cdm_8_mark5_1_addr, cdm_8_mark5_1_data_out, controlled_buffer_1_out, controlled_buffer_2_out,
       iodevice_1_addrout, iodevice_1_memrdout, iodevice_1_memwrout, iodevice_1_wr, iodevice_2_addrout,
       iodevice_2_memrdout, iodevice_2_memwrout, iodevice_2_wr, iodevice_3_addrout, iodevice_3_memrdout,
       iodevice_3_memwrout, iodevice_3_wr, iodevice_4_addrout, iodevice_4_memrdout, iodevice_4_memwrout,
       iodevice_4_wr, iodevice_5_addrout, iodevice_5_memrdout, iodevice_5_memwrout, iodevice_5_wr,
       iodevice_6_addrout, iodevice_6_memrdout, iodevice_6_memwrout, iodevice_7_addrout, iodevice_7_memrdout,
       iodevice_7_memwrout, iodevice_8_addrout, iodevice_8_memrdout, iodevice_8_memwrout, iodevice_9_addrout,
       iodevice_9_memrdout, iodevice_9_memwrout, iodevice_10_addrout, iodevice_10_memrdout,
       iodevice_10_memwrout, iodevice_11_addrout, iodevice_11_memrdout, iodevice_11_memwrout,
       iodevice_12_addrout, iodevice_12_memrdout, iodevice_12_memwrout, iodevice_13_addrout,
       iodevice_13_memrdout, iodevice_13_memwrout, iodevice_14_memrdout, iodevice_14_memwrout,
       iodevice_14_wr, operation, rh, rl;
  wire [15:0] abs_1_out, abs_2_out, divider_1_out, leftOperand, multiplexer_1_out, multiplier_1_cout,
       multiplier_1_out, negator_1_out, rightOperand, shifter_1_out, shifter_1_out_2;
  wire [31:0] shifter_2_out;

  and and_1 (and_1_out, ~reset, clock);  // AND_Gate
  Pull_Resistor pull_resistor_1 (.node(mem));
  CdM_8_mark5 cdm_8_mark5_1 (
    .clock(and_1_out), .addr(cdm_8_mark5_1_addr), .mem_read(doREAD), .mem_cycle(mem),
    .data_out(cdm_8_mark5_1_data_out), .data_in(iodevice_1_memrdout), .reset(reset));  // open: data_inst, r0, r1, r2, r3, PC, SP, PS, IAck, IRQ, vec
  Pull_Resistor #(.pull(1)) pull_resistor_2 (.node(doREAD));
  not not_1 (doWRITE, doREAD);
  and and_2 (and_2_out, doWRITE, mem);
  Register register_1 (.D(iodevice_1_wr), .en(iodevice_1_dowrite), .Q(leftOperand[15:8]), .clk(clock));  // open: clr
  iodevice iodevice_1 (
    .addrIn(cdm_8_mark5_1_addr), .memRdOut(iodevice_1_memrdout), .memWrIn(cdm_8_mark5_1_data_out),
    .doWriteIn(and_2_out), .addrOut(iodevice_1_addrout), .memRdIn(iodevice_2_memrdout),
    .memWrOut(iodevice_1_memwrout), .doWriteOut(iodevice_1_dowriteout), .wr(iodevice_1_wr),
    .doWrite(iodevice_1_dowrite), .neededAddr(8'hfa));  // open: rd
  Register register_2 (.D(iodevice_2_wr), .en(iodevice_2_dowrite), .Q(leftOperand[7:0]), .clk(clock));  // open: clr
  iodevice iodevice_2 (
    .addrIn(iodevice_1_addrout), .memRdOut(iodevice_2_memrdout), .memWrIn(iodevice_1_memwrout),
    .doWriteIn(iodevice_1_dowriteout), .addrOut(iodevice_2_addrout), .memRdIn(iodevice_3_memrdout),
    .memWrOut(iodevice_2_memwrout), .doWriteOut(iodevice_2_dowriteout), .wr(iodevice_2_wr),
    .doWrite(iodevice_2_dowrite), .neededAddr(8'hfb));  // open: rd
  Register register_3 (.D(iodevice_3_wr), .en(iodevice_3_dowrite), .Q(rightOperand[15:8]), .clk(clock));  // open: clr
  iodevice iodevice_3 (
    .addrIn(iodevice_2_addrout), .memRdOut(iodevice_3_memrdout), .memWrIn(iodevice_2_memwrout),
    .doWriteIn(iodevice_2_dowriteout), .addrOut(iodevice_3_addrout), .memRdIn(iodevice_4_memrdout),
    .memWrOut(iodevice_3_memwrout), .doWriteOut(iodevice_3_dowriteout), .rd(rh), .wr(iodevice_3_wr),
    .doWrite(iodevice_3_dowrite), .neededAddr(8'hfc));
  abs abs_1 (.in(leftOperand), .out(abs_1_out), .was_done(abs_1_was_done));
  abs abs_2 (.in(rightOperand), .out(abs_2_out), .was_done(abs_2_was_done));
  Register register_4 (.D(iodevice_4_wr), .en(iodevice_4_dowrite), .Q(rightOperand[7:0]), .clk(clock));  // open: clr
  iodevice iodevice_4 (
    .addrIn(iodevice_3_addrout), .memRdOut(iodevice_4_memrdout), .memWrIn(iodevice_3_memwrout),
    .doWriteIn(iodevice_3_dowriteout), .addrOut(iodevice_4_addrout), .memRdIn(iodevice_5_memrdout),
    .memWrOut(iodevice_4_memwrout), .doWriteOut(iodevice_4_dowriteout), .rd(rl), .wr(iodevice_4_wr),
    .doWrite(iodevice_4_dowrite), .neededAddr(8'hfd));
  xor xor_1 (xor_1_out, abs_1_was_done, abs_2_was_done);
  Register register_5 (.D(iodevice_5_wr), .en(iodevice_5_dowrite), .Q(operation), .clk(clock));  // open: clr
  iodevice iodevice_5 (
    .addrIn(iodevice_4_addrout), .memRdOut(iodevice_5_memrdout), .memWrIn(iodevice_4_memwrout),
    .doWriteIn(iodevice_4_dowriteout), .addrOut(iodevice_5_addrout), .memRdIn(iodevice_6_memrdout),
    .memWrOut(iodevice_5_memwrout), .doWriteOut(iodevice_5_dowriteout), .wr(iodevice_5_wr),
    .doWrite(iodevice_5_dowrite), .neededAddr(8'hfe));  // open: rd
  // Probe on {{16{1'b0}}, abs_1_out}
  Shifter #(.width(32)) shifter_1 (
    .in({{16{1'b0}}, abs_1_out}), .\dist (5'b00111), .out({shifter_1_out_2, shifter_1_out}));
  iodevice iodevice_6 (
    .addrIn(iodevice_5_addrout), .memRdOut(iodevice_6_memrdout), .memWrIn(iodevice_5_memwrout),
    .doWriteIn(iodevice_5_dowriteout), .addrOut(iodevice_6_addrout), .memRdIn(iodevice_7_memrdout),
    .memWrOut(iodevice_6_memwrout), .doWriteOut(iodevice_6_dowriteout), .rd(bx[15:8]), .neededAddr(8'hf2));  // open: wr, doWrite
  iodevice iodevice_7 (
    .addrIn(iodevice_6_addrout), .memRdOut(iodevice_7_memrdout), .memWrIn(iodevice_6_memwrout),
    .doWriteIn(iodevice_6_dowriteout), .addrOut(iodevice_7_addrout), .memRdIn(iodevice_9_memrdout),
    .memWrOut(iodevice_7_memwrout), .doWriteOut(iodevice_7_dowriteout), .rd(bx[7:0]), .neededAddr(8'hf3));  // open: wr, doWrite
  Multiplier #(.width(16)) multiplier_1 (
    .a(abs_1_out), .b(abs_2_out), .out(multiplier_1_out), .cout(multiplier_1_cout));  // open: cin
  iodevice iodevice_8 (
    .addrIn(iodevice_9_addrout), .memRdOut(iodevice_8_memrdout), .memWrIn(iodevice_9_memwrout),
    .doWriteIn(iodevice_9_dowriteout), .addrOut(iodevice_8_addrout), .memRdIn(iodevice_10_memrdout),
    .memWrOut(iodevice_8_memwrout), .doWriteOut(iodevice_8_dowriteout), .rd(by[7:0]), .neededAddr(8'hf5));  // open: wr, doWrite
  iodevice iodevice_9 (
    .addrIn(iodevice_7_addrout), .memRdOut(iodevice_9_memrdout), .memWrIn(iodevice_7_memwrout),
    .doWriteIn(iodevice_7_dowriteout), .addrOut(iodevice_9_addrout), .memRdIn(iodevice_8_memrdout),
    .memWrOut(iodevice_9_memwrout), .doWriteOut(iodevice_9_dowriteout), .rd(by[15:8]), .neededAddr(8'hf4));  // open: wr, doWrite
  Shifter #(.width(32), .shift("ar")) shifter_2 (
    .in({multiplier_1_cout, multiplier_1_out}), .\dist (5'b00111), .out(shifter_2_out));
  Divider #(.width(16)) divider_1 (
    .a(shifter_1_out), .b(abs_2_out), .out(divider_1_out), .upper(shifter_1_out_2));  // open: rem
  iodevice iodevice_10 (
    .addrIn(iodevice_8_addrout), .memRdOut(iodevice_10_memrdout), .memWrIn(iodevice_8_memwrout),
    .doWriteIn(iodevice_8_dowriteout), .addrOut(iodevice_10_addrout), .memRdIn(iodevice_11_memrdout),
    .memWrOut(iodevice_10_memwrout), .doWriteOut(iodevice_10_dowriteout), .rd(vx[15:8]), .neededAddr(8'hf6));  // open: wr, doWrite
  Multiplexer #(.width(16), .enable("false")) multiplexer_1 (
    .in0(shifter_2_out[15:0]), .in1(divider_1_out), .out(multiplexer_1_out), .sel(operation[0]));
  iodevice iodevice_11 (
    .addrIn(iodevice_10_addrout), .memRdOut(iodevice_11_memrdout), .memWrIn(iodevice_10_memwrout),
    .doWriteIn(iodevice_10_dowriteout), .addrOut(iodevice_11_addrout), .memRdIn(iodevice_13_memrdout),
    .memWrOut(iodevice_11_memwrout), .doWriteOut(iodevice_11_dowriteout), .rd(vx[7:0]), .neededAddr(8'hf7));  // open: wr, doWrite
  Negator #(.width(16)) negator_1 (.in(multiplexer_1_out), .out(negator_1_out));
  iodevice iodevice_12 (
    .addrIn(iodevice_13_addrout), .memRdOut(iodevice_12_memrdout), .memWrIn(iodevice_13_memwrout),
    .doWriteIn(iodevice_13_dowriteout), .addrOut(iodevice_12_addrout), .memRdIn(iodevice_14_memrdout),
    .memWrOut(iodevice_12_memwrout), .doWriteOut(iodevice_12_dowriteout), .rd(vy[7:0]), .neededAddr(8'hf9));  // open: wr, doWrite
  iodevice iodevice_13 (
    .addrIn(iodevice_11_addrout), .memRdOut(iodevice_13_memrdout), .memWrIn(iodevice_11_memwrout),
    .doWriteIn(iodevice_11_dowriteout), .addrOut(iodevice_13_addrout), .memRdIn(iodevice_12_memrdout),
    .memWrOut(iodevice_13_memwrout), .doWriteOut(iodevice_13_dowriteout), .rd(vy[15:8]), .neededAddr(8'hf8));  // open: wr, doWrite
  // Probe on {rh, rl}
  Multiplexer #(.width(16), .enable("false")) multiplexer_2 (
    .in0(multiplexer_1_out), .in1(negator_1_out), .out({rh, rl}), .sel(xor_1_out));
  Register register_6 (
    .D(iodevice_14_wr), .en(iodevice_14_dowrite), .Q({vy_2, register_6_q}), .clk(clock));  // open: clr
  iodevice iodevice_14 (
    .addrIn(iodevice_12_addrout), .memRdOut(iodevice_14_memrdout), .memWrIn(iodevice_12_memwrout),
    .doWriteIn(iodevice_12_dowriteout), .addrOut({RAM, iodevice_14_addrout}),
    .memRdIn(controlled_buffer_1_out), .memWrOut(iodevice_14_memwrout), .rd({vy_2, register_6_q}),
    .wr(iodevice_14_wr), .doWrite(iodevice_14_dowrite), .neededAddr({8{1'b1}}));  // open: doWriteOut
  // Probe on {vy_2, register_6_q}
  not not_2 (ROM, RAM);
  and and_3 (and_3_out, RAM, mem);
  assign controlled_buffer_1_out = doREAD ? controlled_buffer_2_out : 8'bz;  // Controlled_Buffer controlled_buffer_1
  assign controlled_buffer_2_out = doWRITE ? iodevice_14_memwrout : 8'bz;  // Controlled_Buffer controlled_buffer_2
  ROM #(.addrWidth(7)) rom_1 (.addr(iodevice_14_addrout), .data(controlled_buffer_2_out), .sel(ROM));
  RAM #(.addrWidth(7)) ram_1 (
    .addr(iodevice_14_addrout), .data(controlled_buffer_2_out), .sel(and_3_out), .clk(clock), .ld(doREAD));  // open: clr
  // Probe on nothing

  // Other names for the same wires on the sheet: clk = clock

  // Notes on the sheet:
  //   contents of rom_1 (hex, n*v repeats v):
  //   cd df d0 f2 b2 8c b3 82 83 d1 1 17 d1 72 26 d0 fa a2 8c a3 d0 f8 d1 fc d6 5f d0 0 d1 fe a4 d0 fc d1
  //   c0 d6 5f d0 c0 d1 fa d6 5f d0 f6 d1 fc d6 5f d0 1 d1 fe a4 d0 f4 b2 8c b3 d1 fc b4 8d b5 17 22 a e5
  //   50 d0 f8 b0 e4 4f d0 7f 12 ee 50 86 2a d0 f8 42 a e0 5b d0 8 38 2 d0 ff a2 d4 b2 a6 8c 8d b2 a6 d7
endmodule

module secret (
  input  a,
  input  b,
  input  [4:0] x,
  input  [4:0] y,
  input  reset,
  output result
);

  wire comparator_1_eq, d, l, not_1_out, ok, pressed, r, u;
  wire [3:0] counter_1_q;
  wire [4:0] adder_1_out, adder_2_out;
  wire [5:0] rom_1_data;

  not not_1 (not_1_out, ok);
  Counter #(.width(4), .max('hf), .trigger("falling")) counter_1 (
    .load(not_1_out), .D(4'b0000), .count(ok), .Q(counter_1_q), .clk(pressed), .clr(reset));  // open: carry
  Adder #(.width(5)) adder_1 (.a(x), .b(5'b10000), .out(adder_1_out));  // open: cin, cout
  Adder #(.width(5)) adder_2 (.a(y), .b(5'b10000), .out(adder_2_out));  // open: cin, cout
  or or_1 (pressed, a, b, r, l, u, d);
  Comparator #(.width(4), .mode("unsigned")) comparator_1 (
    .a(counter_1_q), .b(4'b1010), .eq(comparator_1_eq));  // open: gt, lt
  ROM #(.addrWidth(4), .dataWidth(6)) rom_1 (.addr(counter_1_q), .data(rom_1_data));  // open: sel
  and and_1 (r, adder_1_out[3], ~adder_1_out[4]);  // AND_Gate
  and and_2 (l, ~adder_1_out[3], adder_1_out[4]);  // AND_Gate
  and and_3 (u, adder_2_out[3], ~adder_2_out[4]);  // AND_Gate
  and and_4 (d, ~adder_2_out[3], adder_2_out[4]);  // AND_Gate
  S_R_Flip_Flop s_r_ff_1 (.Q(result), .preset(comparator_1_eq), .reset(reset));  // open: S, clk, R, Qn, en
  Comparator #(.width(6), .mode("unsigned")) comparator_2 (
    .a({d, u, l, r, b, a}), .b(rom_1_data), .eq(ok));  // open: gt, lt

  // Notes on the sheet:
  //   contents of rom_1 (hex, n*v repeats v):
  //   10 10 20 20 8 4 8 4 2 1
endmodule
