// Logisim project video.circ as structural Verilog: 10 circuits, main circuit main
module main (
);

  wire and_1_out, and_2_out, and_3_out, and_4_out, and_5_out, clk, clock_1_out, clock_2_out, doREAD, doWRITE,
       gameOver, iodevice_1_dowriteout, iodevice_2_dowriteout, iodevice_3_dowriteout, iodevice_4_dowriteout,
       iodevice_5_dowrite, mem, rst;
  wire [2:0] register_1_q;
  wire [3:0] ten_1_out_2, ten_1_out_3, ten_2_out_2, ten_2_out_3;
  wire [4:0] joystick_1_y, kinematic_1_ballx, kinematic_1_bally, kinematic_1_leftyout, kinematic_1_rightyout,
       kinematic_1_zero, ry, subtractor_2_out, video_section_1_out_18, video_section_1_out_19,
       video_section_1_out_20, video_section_1_out_21, video_section_1_out_22, video_section_2_out_18,
       video_section_2_out_19, video_section_2_out_20, video_section_2_out_21, video_section_2_out_22,
       video_section_3_out_18, video_section_3_out_19, video_section_3_out_20, video_section_3_out_21,
       video_section_3_out_22;
  wire [7:0] as, bit_extender_1_out, bit_extender_2_out, bs, cdm_8_mark5_1_addr, cdm_8_mark5_1_data_out,
       cdm_8_mark5_1_pc, cdm_8_mark5_1_r0, cdm_8_mark5_1_r1, cdm_8_mark5_1_r2, cdm_8_mark5_1_r3,
       controlled_buffer_1_out, controlled_buffer_2_out, counter_1_q, iodevice_1_addrout,
       iodevice_1_memrdout, iodevice_1_memwrout, iodevice_2_addrout, iodevice_2_memrdout,
       iodevice_2_memwrout, iodevice_3_addrout, iodevice_3_memrdout, iodevice_3_memwrout, iodevice_4_addrout,
       iodevice_4_memrdout, iodevice_4_memwrout, iodevice_5_addrout, iodevice_5_memrdout,
       iodevice_5_memwrout, iodevice_5_wr, subtractor_1_out, video_player_1_control,
       video_section_1_controlin_2, video_section_2_controlin_2, video_section_3_controlin_2, vxy, xb, yb;
  wire [31:0] video_player_1_data, video_section_1_imagedatain_2, video_section_1_out_8,
       video_section_1_out_9, video_section_1_out_10, video_section_1_out_11, video_section_1_out_13,
       video_section_1_out_14, video_section_1_out_15, video_section_1_out_16, video_section_2_imagedatain_2,
       video_section_2_out_8, video_section_2_out_9, video_section_2_out_10, video_section_2_out_11,
       video_section_2_out_13, video_section_2_out_14, video_section_2_out_15, video_section_2_out_16,
       video_section_3_imagedatain_2, video_section_3_out_8, video_section_3_out_9, video_section_3_out_10,
       video_section_3_out_11, video_section_3_out_13, video_section_3_out_14, video_section_3_out_15,
       video_section_3_out_16, video_section_4_out_8, video_section_4_out_9, video_section_4_out_10,
       video_section_4_out_11, video_section_4_out_13, video_section_4_out_14, video_section_4_out_15,
       video_section_4_out_16;

  Clock #(.highDuration(4), .lowDuration(4)) clock_1 (.out(clock_1_out));
  Clock clock_2 (.out(clock_2_out));
  Hex_Digit_Display hex_digit_display_1 (.value(ten_1_out_2));  // open: dp
  Joystick #(.bits(5)) joystick_1 (.y(joystick_1_y));  // open: x
  and and_1 (and_1_out, clock_1_out, ~gameOver);  // AND_Gate
  Subtractor subtractor_1 (.a(as), .b(bs), .out(subtractor_1_out));  // open: bin, bout
  Comparator comparator_1 (.a(subtractor_1_out), .b(8'h4), .gt(gameOver));  // open: eq, lt
  and and_2 (and_2_out, gameOver, clock_2_out);
  Clock clock_3 (.out(clk));
  Hex_Digit_Display hex_digit_display_2 (.value(ten_1_out_3));  // open: dp
  ten ten_1 (.in_1(as), .out_2(ten_1_out_2), .out_3(ten_1_out_3));
  Subtractor #(.width(5)) subtractor_2 (.a({5{1'b1}}), .b(joystick_1_y), .out(subtractor_2_out));  // open: bin, bout
  DotMatrix #(.matrixcols(32), .matrixrows(32)) dotmatrix_1 (
    .col0(video_section_1_out_13), .col1(video_section_1_out_8), .col2(video_section_1_out_14),
    .col3(video_section_1_out_9), .col4(video_section_1_out_15), .col5(video_section_1_out_10),
    .col6(video_section_1_out_16), .col7(video_section_1_out_11), .col8(video_section_2_out_13),
    .col9(video_section_2_out_8), .col10(video_section_2_out_14), .col11(video_section_2_out_9),
    .col12(video_section_2_out_15), .col13(video_section_2_out_10), .col14(video_section_2_out_16),
    .col15(video_section_2_out_11), .col16(video_section_3_out_13), .col17(video_section_3_out_8),
    .col18(video_section_3_out_14), .col19(video_section_3_out_9), .col20(video_section_3_out_15),
    .col21(video_section_3_out_10), .col22(video_section_3_out_16), .col23(video_section_3_out_11),
    .col24(video_section_4_out_13), .col25(video_section_4_out_8), .col26(video_section_4_out_14),
    .col27(video_section_4_out_9), .col28(video_section_4_out_15), .col29(video_section_4_out_10),
    .col30(video_section_4_out_16), .col31(video_section_4_out_11));
  kinematic kinematic_1 (
    .reset(rst), .leftYin(subtractor_2_out), .rightYin(ry), .leftYout(kinematic_1_leftyout),
    .rightYout(kinematic_1_rightyout), .xball(xb), .yball(yb), .vxy(vxy), .scoreA(as), .scoreB(bs),
    .zero(kinematic_1_zero), .ballx(kinematic_1_ballx), .bally(kinematic_1_bally), .clock(and_1_out));
  video_player video_player_1 (
    .enable(gameOver), .clock(and_2_out), .data(video_player_1_data), .control(video_player_1_control));
  Counter counter_1 (.Q(counter_1_q), .clk(and_3_out));  // open: load, D, count, carry, clr
  and and_3 (and_3_out, clk, ~counter_1_q[5]);  // AND_Gate
  video_section video_section_1 (
    .chipID(kinematic_1_zero), .ballX(kinematic_1_ballx), .ballY(kinematic_1_bally),
    .leftbatY(kinematic_1_leftyout), .rightbatY(kinematic_1_rightyout), .out_18(video_section_1_out_18),
    .out_19(video_section_1_out_19), .out_20(video_section_1_out_20), .out_21(video_section_1_out_21),
    .out_22(video_section_1_out_22), .out_13(video_section_1_out_13), .out_8(video_section_1_out_8),
    .out_14(video_section_1_out_14), .out_9(video_section_1_out_9), .out_15(video_section_1_out_15),
    .out_10(video_section_1_out_10), .out_16(video_section_1_out_16), .out_11(video_section_1_out_11),
    .imageDataIn(video_player_1_data), .controlIn(video_player_1_control),
    .controlIn_2(video_section_1_controlin_2), .imageDataIn_2(video_section_1_imagedatain_2));
  not not_1 (rst, counter_1_q[5]);
  video_section video_section_2 (
    .chipID(video_section_1_out_18), .ballX(video_section_1_out_19), .ballY(video_section_1_out_20),
    .leftbatY(video_section_1_out_21), .rightbatY(video_section_1_out_22), .out_18(video_section_2_out_18),
    .out_19(video_section_2_out_19), .out_20(video_section_2_out_20), .out_21(video_section_2_out_21),
    .out_22(video_section_2_out_22), .out_13(video_section_2_out_13), .out_8(video_section_2_out_8),
    .out_14(video_section_2_out_14), .out_9(video_section_2_out_9), .out_15(video_section_2_out_15),
    .out_10(video_section_2_out_10), .out_16(video_section_2_out_16), .out_11(video_section_2_out_11),
    .imageDataIn(video_section_1_imagedatain_2), .controlIn(video_section_1_controlin_2),
    .controlIn_2(video_section_2_controlin_2), .imageDataIn_2(video_section_2_imagedatain_2));
  // Probe on cdm_8_mark5_1_r3
  // Probe on cdm_8_mark5_1_r0
  // Probe on cdm_8_mark5_1_r2
  // Probe on cdm_8_mark5_1_r1
  and and_4 (and_4_out, ~rst, ~gameOver, clk);  // AND_Gate
  video_section video_section_3 (
    .chipID(video_section_2_out_18), .ballX(video_section_2_out_19), .ballY(video_section_2_out_20),
    .leftbatY(video_section_2_out_21), .rightbatY(video_section_2_out_22), .out_18(video_section_3_out_18),
    .out_19(video_section_3_out_19), .out_20(video_section_3_out_20), .out_21(video_section_3_out_21),
    .out_22(video_section_3_out_22), .out_13(video_section_3_out_13), .out_8(video_section_3_out_8),
    .out_14(video_section_3_out_14), .out_9(video_section_3_out_9), .out_15(video_section_3_out_15),
    .out_10(video_section_3_out_10), .out_16(video_section_3_out_16), .out_11(video_section_3_out_11),
    .imageDataIn(video_section_2_imagedatain_2), .controlIn(video_section_2_controlin_2),
    .controlIn_2(video_section_3_controlin_2), .imageDataIn_2(video_section_3_imagedatain_2));
  // Probe on cdm_8_mark5_1_pc
  Pull_Resistor pull_resistor_1 (.node(mem));
  CdM_8_mark5 cdm_8_mark5_1 (
    .clock(and_4_out), .addr(cdm_8_mark5_1_addr), .mem_read(doREAD), .mem_cycle(mem),
    .data_out(cdm_8_mark5_1_data_out), .data_in(iodevice_1_memrdout), .r0(cdm_8_mark5_1_r0),
    .r1(cdm_8_mark5_1_r1), .r2(cdm_8_mark5_1_r2), .r3(cdm_8_mark5_1_r3), .PC(cdm_8_mark5_1_pc));  // open: data_inst, SP, PS, IAck, IRQ, vec, reset
  video_section video_section_4 (
    .chipID(video_section_3_out_18), .ballX(video_section_3_out_19), .ballY(video_section_3_out_20),
    .leftbatY(video_section_3_out_21), .rightbatY(video_section_3_out_22), .out_13(video_section_4_out_13),
    .out_8(video_section_4_out_8), .out_14(video_section_4_out_14), .out_9(video_section_4_out_9),
    .out_15(video_section_4_out_15), .out_10(video_section_4_out_10), .out_16(video_section_4_out_16),
    .out_11(video_section_4_out_11), .imageDataIn(video_section_3_imagedatain_2),
    .controlIn(video_section_3_controlin_2));  // open: out_18, out_19, out_20, out_21, out_22, controlIn_2, imageDataIn_2
  Pull_Resistor #(.pull(1)) pull_resistor_2 (.node(doREAD));
  Hex_Digit_Display hex_digit_display_3 (.value(ten_2_out_2));  // open: dp
  Hex_Digit_Display hex_digit_display_4 (.value(ten_2_out_3));  // open: dp
  ten ten_2 (.in_1(bs), .out_2(ten_2_out_2), .out_3(ten_2_out_3));
  not not_2 (doWRITE, doREAD);
  // Probe on bit_extender_1_out
  and and_5 (and_5_out, doWRITE, mem);
  // Probe on vxy
  assign bit_extender_1_out = {{5{vxy[2]}}, vxy[2:0]};  // Bit_Extender bit_extender_1
  iodevice iodevice_1 (
    .addrIn(cdm_8_mark5_1_addr), .memRdOut(iodevice_1_memrdout), .memWrIn(cdm_8_mark5_1_data_out),
    .doWriteIn(and_5_out), .addrOut(iodevice_1_addrout), .memRdIn(iodevice_2_memrdout),
    .memWrOut(iodevice_1_memwrout), .doWriteOut(iodevice_1_dowriteout), .rd(bit_extender_1_out),
    .neededAddr(8'hfb));  // open: wr, doWrite
  // Probe on bit_extender_2_out
  assign bit_extender_2_out = {{5{vxy[5]}}, vxy[5:3]};  // Bit_Extender bit_extender_2
  iodevice iodevice_2 (
    .addrIn(iodevice_1_addrout), .memRdOut(iodevice_2_memrdout), .memWrIn(iodevice_1_memwrout),
    .doWriteIn(iodevice_1_dowriteout), .addrOut(iodevice_2_addrout), .memRdIn(iodevice_3_memrdout),
    .memWrOut(iodevice_2_memwrout), .doWriteOut(iodevice_2_dowriteout), .rd(bit_extender_2_out),
    .neededAddr(8'hfc));  // open: wr, doWrite
  iodevice iodevice_3 (
    .addrIn(iodevice_2_addrout), .memRdOut(iodevice_3_memrdout), .memWrIn(iodevice_2_memwrout),
    .doWriteIn(iodevice_2_dowriteout), .addrOut(iodevice_3_addrout), .memRdIn(iodevice_4_memrdout),
    .memWrOut(iodevice_3_memwrout), .doWriteOut(iodevice_3_dowriteout), .rd(xb), .neededAddr(8'hfd));  // open: wr, doWrite
  iodevice iodevice_4 (
    .addrIn(iodevice_3_addrout), .memRdOut(iodevice_4_memrdout), .memWrIn(iodevice_3_memwrout),
    .doWriteIn(iodevice_3_dowriteout), .addrOut(iodevice_4_addrout), .memRdIn(iodevice_5_memrdout),
    .memWrOut(iodevice_4_memwrout), .doWriteOut(iodevice_4_dowriteout), .rd(yb), .neededAddr(8'hfe));  // open: wr, doWrite
  // Probe on {ry, register_1_q}
  Register register_1 (.D(iodevice_5_wr), .en(iodevice_5_dowrite), .Q({ry, register_1_q}), .clk(clk));  // open: clr
  iodevice iodevice_5 (
    .addrIn(iodevice_4_addrout), .memRdOut(iodevice_5_memrdout), .memWrIn(iodevice_4_memwrout),
    .doWriteIn(iodevice_4_dowriteout), .addrOut(iodevice_5_addrout), .memRdIn(controlled_buffer_1_out),
    .memWrOut(iodevice_5_memwrout), .rd({ry, register_1_q}), .wr(iodevice_5_wr),
    .doWrite(iodevice_5_dowrite), .neededAddr({8{1'b1}}));  // open: doWriteOut
  assign controlled_buffer_1_out = doREAD ? controlled_buffer_2_out : 8'bz;  // Controlled_Buffer controlled_buffer_1
  assign controlled_buffer_2_out = doWRITE ? iodevice_5_memwrout : 8'bz;  // Controlled_Buffer controlled_buffer_2
  // Probe on controlled_buffer_2_out
  // RAM ram_1: pin names not known; wires that end beside it: iodevice_5_addrout, mem, clk, doREAD, controlled_buffer_2_out

  // Notes on the sheet:
  //   Первые 0x20 тактов зажат ресет
endmodule

module video_chip (
  input  [7:0] controlIn,
  input  [31:0] imageDataIn,
  input  [4:0] chipID,
  input  [4:0] ballX,
  input  [4:0] ballY,
  input  [4:0] leftbatY,
  input  [4:0] rightbatY,
  output [7:0] controlOut,
  output [31:0] imageDataOut,
  output [31:0] out,
  output [4:0] out_11,
  output [4:0] out_12,
  output [4:0] out_13,
  output [4:0] out_14,
  output [4:0] out_15
);

  wire comparator_1_eq;
  wire [31:0] or_1_out, or_2_out, register_1_q, register_2_q, shifter_1_out, shifter_2_out,
       super_decoder_32_1_out, super_decoder_32_2_out, super_decoder_32_3_out;

  Adder #(.width(5)) adder_1 (.a(5'b00001), .b(chipID), .out(out_11));  // open: cin, cout
  Comparator #(.width(5), .mode("unsigned")) comparator_1 (
    .a(controlIn[4:0]), .b(chipID), .eq(comparator_1_eq));  // open: gt, lt
  super_decoder_32 super_decoder_32_1 (.data(ballY), .out(super_decoder_32_1_out), .A(ballX), .B(chipID));
  Register #(.width(32), .trigger("high")) register_1 (
    .D(imageDataIn), .en(controlIn[5]), .Q(register_1_q), .clk(comparator_1_eq));  // open: clr
  super_decoder_32 super_decoder_32_2 (.data(leftbatY), .out(super_decoder_32_2_out), .A(chipID), .B(5'b00011));
  super_decoder_32 super_decoder_32_3 (.data(rightbatY), .out(super_decoder_32_3_out), .A(chipID), .B(5'b11100));
  Register #(.width(32), .trigger("high")) register_2 (
    .D(register_1_q), .en(controlIn[6]), .Q(register_2_q), .clk(controlIn[6]));  // open: clr
  assign or_1_out = super_decoder_32_2_out | super_decoder_32_3_out;  // OR_Gate or_1, 32 bits wide
  Shifter #(.width(32)) shifter_1 (.in(or_1_out), .\dist (5'b00010), .out(shifter_1_out));
  Shifter #(.width(32)) shifter_2 (.in(or_1_out), .\dist (5'b00001), .out(shifter_2_out));
  assign or_2_out = super_decoder_32_1_out | or_1_out | shifter_1_out | shifter_2_out;  // OR_Gate or_2, 32 bits wide
  Multiplexer #(.width(32), .enable("false")) multiplexer_1 (
    .in0(or_2_out), .in1(register_2_q), .out(out), .sel(controlIn[7]));

  assign controlOut = controlIn;
  assign imageDataOut = imageDataIn;
  assign out_12 = ballX;
  assign out_13 = ballY;
  assign out_14 = leftbatY;
  assign out_15 = rightbatY;
endmodule

module super_decoder_32 (
  input  [4:0] data,
  input  [4:0] A,
  input  [4:0] B,
  output [31:0] out
);

  wire comparator_1_eq;

  Decoder #(.select(5), .disabled(0)) decoder_1 (
    .out0(out[0]), .out1(out[1]), .out2(out[2]), .out3(out[3]), .out4(out[4]), .out5(out[5]), .out6(out[6]),
    .out7(out[7]), .out8(out[8]), .out9(out[9]), .out10(out[10]), .out11(out[11]), .out12(out[12]),
    .out13(out[13]), .out14(out[14]), .out15(out[15]), .out16(out[16]), .out17(out[17]), .out18(out[18]),
    .out19(out[19]), .out20(out[20]), .out21(out[21]), .out22(out[22]), .out23(out[23]), .out24(out[24]),
    .out25(out[25]), .out26(out[26]), .out27(out[27]), .out28(out[28]), .out29(out[29]), .out30(out[30]),
    .out31(out[31]), .sel(data), .en(comparator_1_eq));
  Comparator #(.width(5)) comparator_1 (.a(A), .b(B), .eq(comparator_1_eq));  // open: gt, lt
endmodule

module video_section (
  input  [7:0] controlIn,
  input  [31:0] imageDataIn,
  input  [4:0] chipID,
  input  [4:0] ballX,
  input  [4:0] ballY,
  input  [4:0] leftbatY,
  input  [4:0] rightbatY,
  output [31:0] out_8,
  output [31:0] out_9,
  output [31:0] out_10,
  output [31:0] out_11,
  output [7:0] controlIn_2,
  output [31:0] out_13,
  output [31:0] out_14,
  output [31:0] out_15,
  output [31:0] out_16,
  output [31:0] imageDataIn_2,
  output [4:0] out_18,
  output [4:0] out_19,
  output [4:0] out_20,
  output [4:0] out_21,
  output [4:0] out_22
);

  wire [4:0] video_chip_1_out_11, video_chip_1_out_12, video_chip_1_out_13, video_chip_1_out_14,
       video_chip_1_out_15, video_chip_2_out_11, video_chip_2_out_12, video_chip_2_out_13,
       video_chip_2_out_14, video_chip_2_out_15, video_chip_3_out_11, video_chip_3_out_12,
       video_chip_3_out_13, video_chip_3_out_14, video_chip_3_out_15, video_chip_4_out_11,
       video_chip_4_out_12, video_chip_4_out_13, video_chip_4_out_14, video_chip_4_out_15,
       video_chip_5_out_11, video_chip_5_out_12, video_chip_5_out_13, video_chip_5_out_14,
       video_chip_5_out_15, video_chip_6_out_11, video_chip_6_out_12, video_chip_6_out_13,
       video_chip_6_out_14, video_chip_6_out_15, video_chip_8_out_11, video_chip_8_out_12,
       video_chip_8_out_13, video_chip_8_out_14, video_chip_8_out_15;
  wire [7:0] video_chip_1_controlout, video_chip_2_controlout, video_chip_3_controlout,
       video_chip_4_controlout, video_chip_5_controlout, video_chip_6_controlout, video_chip_8_controlout;
  wire [31:0] video_chip_1_imagedataout, video_chip_2_imagedataout, video_chip_3_imagedataout,
       video_chip_4_imagedataout, video_chip_5_imagedataout, video_chip_6_imagedataout,
       video_chip_8_imagedataout;

  video_chip video_chip_1 (
    .out_11(video_chip_1_out_11), .out_12(video_chip_1_out_12), .ballX(ballX), .out_13(video_chip_1_out_13),
    .ballY(ballY), .out_14(video_chip_1_out_14), .leftbatY(leftbatY), .out_15(video_chip_1_out_15),
    .rightbatY(rightbatY), .out(out_13), .chipID(chipID), .imageDataIn(imageDataIn), .controlIn(controlIn),
    .controlOut(video_chip_1_controlout), .imageDataOut(video_chip_1_imagedataout));
  video_chip video_chip_2 (
    .out_11(video_chip_2_out_11), .out_12(video_chip_2_out_12), .ballX(video_chip_1_out_12),
    .out_13(video_chip_2_out_13), .ballY(video_chip_1_out_13), .out_14(video_chip_2_out_14),
    .leftbatY(video_chip_1_out_14), .out_15(video_chip_2_out_15), .rightbatY(video_chip_1_out_15),
    .out(out_8), .chipID(video_chip_1_out_11), .imageDataIn(video_chip_1_imagedataout),
    .controlIn(video_chip_1_controlout), .controlOut(video_chip_2_controlout),
    .imageDataOut(video_chip_2_imagedataout));
  video_chip video_chip_3 (
    .out_11(video_chip_3_out_11), .out_12(video_chip_3_out_12), .ballX(video_chip_2_out_12),
    .out_13(video_chip_3_out_13), .ballY(video_chip_2_out_13), .out_14(video_chip_3_out_14),
    .leftbatY(video_chip_2_out_14), .out_15(video_chip_3_out_15), .rightbatY(video_chip_2_out_15),
    .out(out_14), .chipID(video_chip_2_out_11), .imageDataIn(video_chip_2_imagedataout),
    .controlIn(video_chip_2_controlout), .controlOut(video_chip_3_controlout),
    .imageDataOut(video_chip_3_imagedataout));
  video_chip video_chip_4 (
    .out_11(video_chip_4_out_11), .out_12(video_chip_4_out_12), .ballX(video_chip_3_out_12),
    .out_13(video_chip_4_out_13), .ballY(video_chip_3_out_13), .out_14(video_chip_4_out_14),
    .leftbatY(video_chip_3_out_14), .out_15(video_chip_4_out_15), .rightbatY(video_chip_3_out_15),
    .out(out_9), .chipID(video_chip_3_out_11), .imageDataIn(video_chip_3_imagedataout),
    .controlIn(video_chip_3_controlout), .controlOut(video_chip_4_controlout),
    .imageDataOut(video_chip_4_imagedataout));
  video_chip video_chip_5 (
    .out_11(video_chip_5_out_11), .out_12(video_chip_5_out_12), .ballX(video_chip_4_out_12),
    .out_13(video_chip_5_out_13), .ballY(video_chip_4_out_13), .out_14(video_chip_5_out_14),
    .leftbatY(video_chip_4_out_14), .out_15(video_chip_5_out_15), .rightbatY(video_chip_4_out_15),
    .out(out_15), .chipID(video_chip_4_out_11), .imageDataIn(video_chip_4_imagedataout),
    .controlIn(video_chip_4_controlout), .controlOut(video_chip_5_controlout),
    .imageDataOut(video_chip_5_imagedataout));
  video_chip video_chip_6 (
    .out_11(video_chip_6_out_11), .out_12(video_chip_6_out_12), .ballX(video_chip_5_out_12),
    .out_13(video_chip_6_out_13), .ballY(video_chip_5_out_13), .out_14(video_chip_6_out_14),
    .leftbatY(video_chip_5_out_14), .out_15(video_chip_6_out_15), .rightbatY(video_chip_5_out_15),
    .out(out_10), .chipID(video_chip_5_out_11), .imageDataIn(video_chip_5_imagedataout),
    .controlIn(video_chip_5_controlout), .controlOut(video_chip_6_controlout),
    .imageDataOut(video_chip_6_imagedataout));
  video_chip video_chip_7 (
    .out_11(out_18), .out_12(out_19), .ballX(video_chip_8_out_12), .out_13(out_20),
    .ballY(video_chip_8_out_13), .out_14(out_21), .leftbatY(video_chip_8_out_14), .out_15(out_22),
    .rightbatY(video_chip_8_out_15), .out(out_11), .chipID(video_chip_8_out_11),
    .imageDataIn(video_chip_8_imagedataout), .controlIn(video_chip_8_controlout), .controlOut(controlIn_2),
    .imageDataOut(imageDataIn_2));
  video_chip video_chip_8 (
    .out_11(video_chip_8_out_11), .out_12(video_chip_8_out_12), .ballX(video_chip_6_out_12),
    .out_13(video_chip_8_out_13), .ballY(video_chip_6_out_13), .out_14(video_chip_8_out_14),
    .leftbatY(video_chip_6_out_14), .out_15(video_chip_8_out_15), .rightbatY(video_chip_6_out_15),
    .out(out_16), .chipID(video_chip_6_out_11), .imageDataIn(video_chip_6_imagedataout),
    .controlIn(video_chip_6_controlout), .controlOut(video_chip_8_controlout),
    .imageDataOut(video_chip_8_imagedataout));
endmodule

module reflect (
  input  [2:0] oldv,
  output [2:0] newv
);

  wire comparator_1_eq;
  wire [2:0] adder_1_out, negator_1_out;

  // Probe on oldv
  Adder #(.width(3)) adder_1 (.a(3'b001), .b(negator_1_out), .out(adder_1_out));  // open: cin, cout
  // Probe on negator_1_out
  Negator #(.width(3)) negator_1 (.in(oldv), .out(negator_1_out));
  Comparator #(.width(3)) comparator_1 (.a(oldv), .b(3'b100), .eq(comparator_1_eq));  // open: gt, lt
  // Probe on newv
  Multiplexer #(.width(3), .enable("false")) multiplexer_1 (
    .in0(negator_1_out), .in1(adder_1_out), .out(newv), .sel(comparator_1_eq));
endmodule

module inrange (
  input  [4:0] yball,
  input  [4:0] ybat,
  output out_3
);

  wire comparator_1_eq, comparator_2_eq, comparator_3_eq;
  wire [4:0] adder_1_out, adder_2_out;

  Adder #(.width(5)) adder_1 (.a(ybat), .b(5'b00001), .out(adder_1_out));  // open: cin, cout
  Adder #(.width(5)) adder_2 (.a(ybat), .b(5'b00010), .out(adder_2_out));  // open: cin, cout
  Comparator #(.width(5)) comparator_1 (.a(yball), .b(ybat), .eq(comparator_1_eq));  // open: gt, lt
  Comparator #(.width(5)) comparator_2 (.a(yball), .b(adder_1_out), .eq(comparator_2_eq));  // open: gt, lt
  Comparator #(.width(5)) comparator_3 (.a(yball), .b(adder_2_out), .eq(comparator_3_eq));  // open: gt, lt
  or or_1 (out_3, comparator_1_eq, comparator_2_eq, comparator_3_eq);
endmodule

module kinematic (
  input  clock,
  input  reset,
  input  [4:0] leftYin,
  input  [4:0] rightYin,
  output [4:0] leftYout,
  output [4:0] rightYout,
  output [7:0] xball,
  output [7:0] yball,
  output [7:0] vxy,
  output [7:0] scoreA,
  output [7:0] scoreB,
  output [4:0] zero,
  output [4:0] ballx,
  output [4:0] bally
);

  wire adder_5_cout, adder_6_cout, adder_9_cout, adder_10_cout, and_1_out, Bcontact, hitA, hitB,
       inrange_1_out_3, inrange_2_out_3, LBcontact, not_1_out, not_2_out, not_3_out, not_4_out, not_5_out,
       not_6_out, or_1_out, or_2_out, or_3_out, or_4_out, RBcontact, xor_3_out, xor_4_out, xrefl, yrefl;
  wire [2:0] multiplexer_3_out, multiplexer_4_out, reflect_1_newv, reflect_2_newv;
  wire [7:0] adder_1_out, adder_2_out, adder_3_out, adder_4_out, adder_7_out, adder_8_out, longVX, longVY,
       multiplexer_1_out, multiplexer_2_out;

  Adder adder_1 (.a({ballx, xball[2:0]}), .b(longVX), .out(adder_1_out));  // open: cin, cout
  Multiplexer #(.width(8), .enable("false")) multiplexer_1 (
    .in0(adder_1_out), .in1(8'hc0), .out(multiplexer_1_out), .sel(reset));
  not not_1 (not_1_out, xrefl);
  not not_2 (not_2_out, Bcontact);
  Adder adder_2 (.a({bally, yball[2:0]}), .b(longVY), .out(adder_2_out));  // open: cin, cout
  not not_3 (not_3_out, xrefl);
  Adder adder_3 (.a(scoreA), .b(8'h1), .out(adder_3_out));  // open: cin, cout
  Register register_1 (.D(adder_3_out), .en(hitA), .Q(scoreA), .clk(clock), .clr(reset));
  Register register_2 (.D(adder_4_out), .en(hitB), .Q(scoreB), .clk(clock), .clr(reset));
  Adder adder_4 (.a(scoreB), .b(8'h1), .out(adder_4_out));  // open: cin, cout
  and and_1 (and_1_out, not_1_out, not_2_out);
  or or_1 (or_1_out, and_1_out, reset);
  Multiplexer #(.width(8), .enable("false")) multiplexer_2 (
    .in0(adder_2_out), .in1(8'hc0), .out(multiplexer_2_out), .sel(reset));
  or or_2 (or_2_out, not_3_out, reset);
  not not_4 (not_4_out, ballx[4]);
  Register #(.trigger("falling")) xreg (
    .D(multiplexer_1_out), .en(or_1_out), .Q({ballx, xball[2:0]}), .clk(clock));  // open: clr
  Register #(.trigger("falling")) yreg (
    .D(multiplexer_2_out), .en(or_2_out), .Q({bally, yball[2:0]}), .clk(clock));  // open: clr
  reflect reflect_1 (.oldv(vxy[2:0]), .newv(reflect_1_newv));
  Register #(.width(5), .trigger("falling")) rightYreg (
    .D(rightYin), .en(not_4_out), .Q(rightYout), .clk(clock));  // open: clr
  Multiplexer #(.width(3), .enable("false")) multiplexer_3 (
    .in0(reflect_1_newv), .in1(3'b110), .out(multiplexer_3_out), .sel(reset));
  or or_3 (or_3_out, reset, Bcontact, xrefl);
  reflect reflect_2 (.oldv(vxy[5:3]), .newv(reflect_2_newv));
  Multiplexer #(.width(3), .enable("false")) multiplexer_4 (
    .in0(reflect_2_newv), .in1(3'b001), .out(multiplexer_4_out), .sel(reset));
  or or_4 (or_4_out, yrefl, reset);
  Register #(.width(3)) vx (.D(multiplexer_3_out), .en(or_3_out), .Q(vxy[2:0]), .clk(clock));  // open: clr
  Register #(.width(3)) vy (.D(multiplexer_4_out), .en(or_4_out), .Q(vxy[5:3]), .clk(clock));  // open: clr
  assign longVX = {{5{vxy[2]}}, vxy[2:0]};  // Bit_Extender bit_extender_1
  assign longVY = {{5{vxy[5]}}, vxy[5:3]};  // Bit_Extender bit_extender_2
  Adder adder_5 (.a({ballx, xball[2:0]}), .b(longVX), .cout(adder_5_cout));  // open: out, cin
  not not_5 (not_5_out, Bcontact);
  xor xor_1 (xrefl, adder_5_cout, longVX[7]);
  and and_2 (hitB, xrefl, not_5_out, longVX[7]);
  not not_6 (not_6_out, longVX[7]);
  Adder adder_6 (.a({bally, yball[2:0]}), .b(longVY), .cout(adder_6_cout));  // open: out, cin
  and and_3 (hitA, xrefl, not_5_out, not_6_out);
  xor xor_2 (yrefl, adder_6_cout, longVY[7]);
  Adder adder_7 (.a({ballx, xball[2:0]}), .b(8'he4), .out(adder_7_out));  // open: cin, cout
  Adder adder_8 (.a({ballx, xball[2:0]}), .b(8'h1c), .out(adder_8_out));  // open: cin, cout
  Adder adder_9 (.a(adder_7_out), .b(longVX), .cout(adder_9_cout));  // open: out, cin
  inrange inrange_1 (.yball(bally), .ybat(leftYin), .out_3(inrange_1_out_3));
  Adder adder_10 (.a(adder_8_out), .b(longVX), .cout(adder_10_cout));  // open: out, cin
  inrange inrange_2 (.yball(bally), .ybat(rightYout), .out_3(inrange_2_out_3));
  xor xor_3 (xor_3_out, adder_9_cout, longVX[7]);
  xor xor_4 (xor_4_out, adder_10_cout, longVX[7]);
  and and_4 (LBcontact, xor_3_out, inrange_1_out_3);
  and and_5 (RBcontact, xor_4_out, inrange_2_out_3);
  or or_5 (Bcontact, LBcontact, RBcontact);

  assign leftYout = leftYin;
  assign vxy[7:6] = 2'b00;
  assign xball[7:3] = ballx;
  assign yball[7:3] = bally;
  assign zero = {5{1'b0}};

  // Other names for the same wires on the sheet: clk = clock; vxneg = longVX[7]; vyneg = longVY[7]; scA[7:0] = scoreA;
  //   scB[7:0] = scoreB; xreg[7:0] = {ballx, xball[2:0]}; yreg[7:0] = {bally, yball[2:0]}
endmodule

module ten (
  input  [7:0] in_1,
  output [3:0] out_2,
  output [3:0] out_3
);

  wire [7:4] divider_1_out, divider_1_rem;

  // Probe on in_1
  Divider divider_1 (.a(in_1), .b(8'ha), .out({divider_1_out, out_2}), .rem({divider_1_rem, out_3}));  // open: upper
  // Probe on out_2
  // Probe on out_3
endmodule

module iodevice (
  input  [7:0] rd,
  input  [7:0] addrIn,
  input  [7:0] memRdIn,
  input  [7:0] memWrIn,
  input  doWriteIn,
  input  [7:0] neededAddr,
  output [7:0] wr,
  output doWrite,
  output [7:0] addrOut,
  output [7:0] memRdOut,
  output [7:0] memWrOut,
  output doWriteOut
);

  wire comparator_1_eq;

  Multiplexer #(.width(8), .enable("false")) multiplexer_1 (
    .in0(memRdIn), .in1(rd), .out(memRdOut), .sel(comparator_1_eq));
  Comparator #(.mode("unsigned")) comparator_1 (.a(addrIn), .b(neededAddr), .eq(comparator_1_eq));  // open: gt, lt
  and and_1 (doWrite, comparator_1_eq, doWriteIn);

  assign addrOut = addrIn;
  assign doWriteOut = doWriteIn;
  assign memWrOut = memWrIn;
  assign wr = memWrIn;
endmodule

module video_player (
  input  enable,
  input  clock,
  output [31:0] data,
  output [7:0] control
);

  wire [23:0] adder_1_out;
  wire [23:5] register_1_q;

  and and_1 (control[5], enable, clock);
  Adder #(.width(24)) adder_1 (.a(24'h1), .b({register_1_q, control[4:0]}), .out(adder_1_out));  // open: cin, cout
  Register #(.width(24)) register_1 (
    .D(adder_1_out), .en(control[5]), .Q({register_1_q, control[4:0]}), .clk(control[5]));  // open: clr
  ROM #(.addrWidth(24), .dataWidth(32)) rom_1 (.addr({register_1_q, control[4:0]}), .data(data), .sel(1'b1));
  Comparator #(.width(5), .mode("unsigned")) comparator_1 (
    .a(control[4:0]), .b({5{1'b1}}), .eq(control[6]));  // open: gt, lt

  assign control[7] = enable;

  // Notes on the sheet:
  //   contents of rom_1 (hex, n*v repeats v):
  //   31*0 1f800 30*0 1f800 10000 29*0 1f800 10000 10000 28*0 1f800 10000 10000 1f800 27*0 1f800 10000
  //   10000 1f800 27*0 1f800 10000 10000 1f800 0 1f800 25*0 1f800 10000 10000 1f800 0 1f800 10800 24*0
  //   1f800 10000 10000 1f800 0 1f800 10800 101f800 23*0 1f800 10000 10000 1f800 0 1f800 10800 101f800
  //   1000000 22*0 1f800 10000 10000 1f800 0 1f800 10800 101f800 1000000 1f9f800 21*0 1f800 10000 10000
  //   1f800 0 1f800 10800 101f800 1000000 1f9f800 1012800 20*0 1f800 10000 10000 1f800 0 1f800 10800
  //   101f800 1000000 1f9f800 1012800 1013800 19*0 1f800 10000 10000 1f800 0 1f800 10800 101f800 1000000
  //   1f9f800 1012800 1013800 1000000 18*0 1f800 10000 10000 1f800 0 1f800 10800 101f800 1000000 1f9f800
  //   1012800 1013800 1000000 1f800 17*0 1f800 10000 10000 1f800 0 1f800 10800 101f800 1000000 1f9f800
  //   1012800 1013800 1000000 1f800 14800 16*0 1f800 10000 10000 1f800 0 1f800 10800 101f800 1000000
  //   1f9f800 1012800 1013800 1000000 1f800 14800 1f80000 15*0 1f800 10000 10000 1f800 0 1f800 10800
  //   101f800 1000000 1f9f800 1012800 1013800 1000000 1f800 14800 1f80000 280c00 14*0 1f800 10000 10000
  //   1f800 0 1f800 10800 101f800 1000000 1f9f800 1012800 1013800 1000000 1f800 14800 1f80000 280c00
  //   29f800 13*0 1f800 10000 10000 1f800 0 1f800 10800 101f800 1000000 1f9f800 1012800 1013800 1000000
  //   1f800 14800 1f80000 280c00 29f800 390800 12*0 1f800 10000 10000 1f800 0 1f800 10800 101f800 1000000
  //   1f9f800 1012800 1013800 1000000 1f800 14800 1f80000 280c00 29f800 390800 1f800 11*0 1f800 10000
  //   10000 1f800 0 1f800 10800 101f800 1000000 1f9f800 1012800 1013800 1000000 1f800 14800 1f80000 280c00
  //   29f800 390800 1f800 c00 10*0 1f800 10000 10000 1f800 0 1f800 10800 101f800 1000000 1f9f800 1012800
  //   1013800 1000000 1f800 14800 1f80000 280c00 29f800 390800 1f800 c00 1f80000 9*0 1f800 10000 10000
  //   1f800 0 1f800 10800 101f800 1000000 1f9f800 1012800 1013800 1000000 1f800 14800 1f80000 280c00
  //   29f800 390800 1f800 c00 1f80000 1f800 8*0 1f800 10000 10000 1f800 0 1f800 10800 101f800 1000000
  //   1f9f800 1012800 1013800 1000000 1f800 14800 1f80000 280c00 29f800 390800 1f800 c00 1f80000 1f800
  //   2000 7*0 1f800 10000 10000 1f800 0 1f800 10800 101f800 1000000 1f9f800 1012800 1013800 1000000 1f800
  //   14800 1f80000 280c00 29f800 390800 1f800 c00 1f80000 1f800 2000 4000 6*0 1f800 10000 10000 1f800 0
  //   1f800 10800 101f800 1000000 1f9f800 1012800 1013800 1000000 1f800 14800 1f80000 280c00 29f800 390800
  //   1f800 c00 1f80000 1f800 2000 4000 1f800 5*0 1f800 10000 10000 1f800 0 1f800 10800 101f800 1000000
  //   1f9f800 1012800 1013800 1000000 1f800 14800 1f80000 280c00 29f800 390800 1f800 c00 1f80000 1f800
  //   2000 4000 1f800 5*0 1f800 10000 10000 1f800 0 1f800 10800 101f800 1000000 1f9f800 1012800 1013800
  //   1000000 1f800 14800 1f80000 280c00 29f800 390800 1f800 c00 1f80000 1f800 2000 4000 1f800 0 800 0 0 0
  //   1f800 10000 10000 1f800 0 1f800 10800 101f800 1000000 1f9f800 1012800 1013800 1000000 1f800 14800
  //   1f80000 280c00 29f800 390800 1f800 c00 1f80000 1f800 2000 4000 1f800 0 800 1000 0 0 1f800 10000
  //   10000 1f800 0 1f800 10800 101f800 1000000 1f9f800 1012800 1013800 1000000 1f800 14800 1f80000 280c00
  //   29f800 390800 1f800 c00 1f80000 1f800 2000 4000 1f800 0 800 1000 1e000 0 1f800 10000 10000 1f800 0
  //   1f800 10800 101f800 1000000 1f9f800 1012800 1013800 1000000 1f800 14800 1f80000 280c00 29f800 390800
  //   1f800 c00 1f80000 1f800 2000 4000 1f800 0 800 1000 1e000 10000 1f800 10000 10000 1f800 0 1f800 10800
  //   101f800 1000000 1f9f800 1012800 1013800 1000000 1f800 14800 1f80000 280c00 29f800 390800 1f800 c00
  //   1f80000 1f800 2000 4000 1f800 0 800 1000 1e000 10000 1f800 1f800 10000 10000 1f800 0 1f800 10800
  //   101f800 1000000 1f9f800 1012800 1013800 1000000 1f800 14800 1f80000 280c00 29f800 390800 1f800 c00
  //   1f80000 1f800 2000 4000 1f800 0 800 1000 1e000 10000 1f800 30000 30000 3f800 0 3f800 30800 203f800
  //   2000000 3f3f800 2032800 2033800 2000000 3f800 34800 3f00000 3f00000 500c00 53f800 730800 3f800 c00
  //   3f00000 3f800 2000 4000 3f800 0 800 1000 3e000 30000 3f800 10000 1fc00 0 0 1fc00 10c00 201fc00
  //   2000000 3f9fc00 2012c00 2013c00 2000000 2000000 1fc00 14c00 3f80000 580e00 59fc0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
endmodule
